// Logisim project 8bitProcessor.circ as structural Verilog: 5 circuits, main circuit main
module main (
);

  wire arithmetic_unit_1_p2, arithmetic_unit_1_p5, arithmetic_unit_3_p2, arithmetic_unit_3_p3, fanout_1_p1,
       fanout_1_p2, fanout_1_p3, fanout_1_p4, fanout_2_p1, fanout_2_p2, fanout_2_p3, fanout_2_p4,
       fanout_3_p2, fanout_3_p3, fanout_4_p2, fanout_5_p5, fanout_6_p3, MAN_out, multiplexor_1_p2,
       multiplexor_1_p3, multiplexor_1_p5, multiplexor_2_p2, multiplexor_2_p4, multiplexor_3_p2,
       multiplexor_4_p3, multiplexor_5_p1, multiplexor_6_p1, ram_1_p1, ram_1_p2, ram_1_p5, ram_1_p7,
       ram_1_p8, register_4_p2, register_4_p3, register_6_p3, RST_out;
  wire [3:0] arithmetic_unit_1_p1, arithmetic_unit_1_p3, arithmetic_unit_1_p4, control_1_amuxc,
       control_1_auc, control_1_aucc, control_1_bmuxc, control_1_bregc, control_1_ldoreg, control_1_pcc,
       control_1_pfix_2, control_1_ramc, control_1_rmuxc, control_1_rregc, decoder_1_add, decoder_1_br,
       decoder_1_brb, decoder_1_brn, decoder_1_brz, decoder_1_exec_2, decoder_1_ldac, decoder_1_ldai,
       decoder_1_ldam, decoder_1_ldap, decoder_1_ldbc, decoder_1_ldbi, decoder_1_ldbm, decoder_1_pfix,
       decoder_1_stai, decoder_1_stam, decoder_1_sub, fanout_1_p5, fanout_2_p5,
       instr_and_operand_register_1_todecode_fn, multiplexor_1_p4, multiplexor_3_p4, multiplexor_5_p2,
       multiplexor_6_p2, register_1_p2, timing_1_exec, timing_1_fetch, timing_1_inc, timing_1_phase_1,
       timing_1_phase_2;

  // Probe on {arithmetic_unit_1_p3, arithmetic_unit_1_p4}
  Button MAN (.out(MAN_out));
  Timing timing_1 (
    .phase_1(timing_1_phase_1), .phase_2(timing_1_phase_2), .FETCH(timing_1_fetch), .INC(timing_1_inc),
    .EXEC(timing_1_exec), .RESET(RST_out), .MANUAL(MAN_out));
  Button RST (.out(RST_out));
  Decoder decoder_1 (
    .EXEC_2(decoder_1_exec_2), .FN(instr_and_operand_register_1_todecode_fn), .LDAM(decoder_1_ldam),
    .LDBM(decoder_1_ldbm), .STAM(decoder_1_stam), .LDAC(decoder_1_ldac), .LDBC(decoder_1_ldbc),
    .LDAP(decoder_1_ldap), .LDAI(decoder_1_ldai), .LDBI(decoder_1_ldbi), .STAI(decoder_1_stai),
    .BR(decoder_1_br), .BRZ(decoder_1_brz), .BRN(decoder_1_brn), .BRB(decoder_1_brb), .ADD(decoder_1_add),
    .SUB(decoder_1_sub), .PFIX(decoder_1_pfix), .EXEC(timing_1_exec));
  // Arithmetic_Unit arithmetic_unit_1: pin names not known; wires that end beside it: arithmetic_unit_1_p1, arithmetic_unit_1_p2, arithmetic_unit_1_p3, arithmetic_unit_1_p4, arithmetic_unit_1_p5
  // Fanout fanout_1: pin names not known; wires that end beside it: fanout_1_p1, fanout_1_p2, fanout_1_p3, fanout_1_p4, fanout_1_p5
  // Fanout fanout_2: pin names not known; wires that end beside it: fanout_2_p1, fanout_2_p2, fanout_2_p3, fanout_2_p4, fanout_2_p5
  // Fanout fanout_3: pin names not known; wires that end beside it: arithmetic_unit_1_p4, fanout_3_p2, fanout_3_p3
  // Fanout fanout_4: pin names not known; wires that end beside it: arithmetic_unit_1_p2, fanout_4_p2, arithmetic_unit_1_p3
  // Register register_1: pin names not known; wires that end beside it: fanout_2_p2, register_1_p2
  // Register register_2: pin names not known; wires that end beside it: fanout_1_p2
  Control control_1 (
    .FETCH(timing_1_fetch), .INCPC(timing_1_inc), .LDAM(decoder_1_ldam), .LDBM(decoder_1_ldbm),
    .STAM(decoder_1_stam), .LDAC(decoder_1_ldac), .LDBC(decoder_1_ldbc), .LDAP(decoder_1_ldap),
    .LDAI(decoder_1_ldai), .LDBI(decoder_1_ldbi), .STAI(decoder_1_stai), .BR(decoder_1_br),
    .BRZ(decoder_1_brz), .BRN(decoder_1_brn), .BRB(decoder_1_brb), .ADD(decoder_1_add), .SUB(decoder_1_sub),
    .PFIX(decoder_1_pfix), .phi1(timing_1_phase_1), .phi2(timing_1_phase_2), .RAMC(control_1_ramc),
    .AUCC(control_1_aucc), .AREGC(register_1_p2), .PCC(control_1_pcc), .AMUXC(control_1_amuxc),
    .BREGC(control_1_bregc), .BMUXC(control_1_bmuxc), .PFIX_2(control_1_pfix_2), .LDOREG(control_1_ldoreg),
    .AUC(control_1_auc), .RMUXC(control_1_rmuxc), .RREGC(control_1_rregc), .Cond(arithmetic_unit_1_p1));
  // RAM ram_1: pin names not known; wires that end beside it: ram_1_p1, ram_1_p2, ram_1_p1, arithmetic_unit_1_p3, ram_1_p5, arithmetic_unit_1_p4, ram_1_p7, ram_1_p8
  // Arithmetic_Unit arithmetic_unit_2: pin names not known; wires that end beside it: arithmetic_unit_1_p5, fanout_3_p2, control_1_aucc
  // Multiplexor multiplexor_1: pin names not known; wires that end beside it: fanout_4_p2, multiplexor_1_p2, multiplexor_1_p3, multiplexor_1_p4, multiplexor_1_p5, multiplexor_1_p3
  // Register register_3: pin names not known; wires that end beside it: multiplexor_1_p2, fanout_1_p3
  // Register register_4: pin names not known; wires that end beside it: fanout_1_p1, register_4_p2, register_4_p3
  // Multiplexor multiplexor_2: pin names not known; wires that end beside it: ram_1_p2, multiplexor_2_p2, register_4_p2, multiplexor_2_p4
  // Fanout fanout_5: pin names not known; wires that end beside it: control_1_ramc, arithmetic_unit_1_p3, ram_1_p8, multiplexor_2_p2, fanout_5_p5, fanout_5_p5
  // Arithmetic_Unit arithmetic_unit_3: pin names not known; wires that end beside it: arithmetic_unit_1_p4, arithmetic_unit_3_p2, arithmetic_unit_3_p3, multiplexor_1_p3, multiplexor_1_p5
  // Multiplexor multiplexor_3: pin names not known; wires that end beside it: fanout_3_p3, multiplexor_3_p2, arithmetic_unit_3_p3, multiplexor_3_p4, control_1_amuxc
  // Register register_5: pin names not known; wires that end beside it: multiplexor_3_p2, fanout_2_p3, control_1_pcc
  // Register register_6: pin names not known; wires that end beside it: register_4_p3, fanout_2_p1, register_6_p3, control_1_rregc
  // Multiplexor multiplexor_4: pin names not known; wires that end beside it: multiplexor_2_p4, ram_1_p5, multiplexor_4_p3, register_6_p3, control_1_rmuxc
  // Fanout fanout_6: pin names not known; wires that end beside it: ram_1_p7, multiplexor_4_p3, fanout_6_p3, fanout_6_p3
  // Arithmetic_Unit arithmetic_unit_4: pin names not known; wires that end beside it: arithmetic_unit_3_p3, arithmetic_unit_3_p2, control_1_auc, arithmetic_unit_3_p2
  // Multiplexor multiplexor_5: pin names not known; wires that end beside it: multiplexor_5_p1, multiplexor_5_p2, multiplexor_1_p5, arithmetic_unit_3_p3, multiplexor_1_p5, multiplexor_1_p3
  // Register register_7: pin names not known; wires that end beside it: multiplexor_5_p1, fanout_1_p4
  // Multiplexor multiplexor_6: pin names not known; wires that end beside it: multiplexor_6_p1, multiplexor_6_p2, arithmetic_unit_3_p2, control_1_bmuxc
  // Register register_8: pin names not known; wires that end beside it: multiplexor_6_p1, fanout_2_p4, control_1_bregc
  Instr_And_Operand_Register instr_and_operand_register_1 (
    .toDecode_FN(instr_and_operand_register_1_todecode_fn), .exec(decoder_1_exec_2),
    .Load_Reg(control_1_ldoreg), .PFix(control_1_pfix_2), .oreg_highB(multiplexor_5_p2),
    .oreg_highA(multiplexor_1_p4), .oreg_lowB(multiplexor_6_p2), .oreg_lowA(multiplexor_3_p4),
    .RHigh(fanout_1_p5), .RLow(fanout_2_p5));  // open: oreg_high0, oreg_high1, oreg_high3, oreg_high4, oreg_low0, oreg_low1, oreg_low3, oreg_low4

  // Notes on the sheet:
  //   areg
  //   pc
  //   rreg
  //   rmux
  //   breg
endmodule

module Timing (
  input  RESET,
  input  MANUAL,
  output [3:0] FETCH,
  output [3:0] INC,
  output [3:0] EXEC,
  output [3:0] phase_1,
  output [3:0] phase_2
);

  wire demultiplexer_1_p2;

  // Demultiplexer demultiplexer_1: pin names not known; wires that end beside it: 4'b0001, demultiplexer_1_p2, FETCH, INC, EXEC
  // Register register_1: pin names not known; wires that end beside it: phase_1
  // Register register_2: pin names not known; wires that end beside it: phase_2
  // Arithmetic_Unit arithmetic_unit_1: pin names not known; wires that end beside it: demultiplexer_1_p2, 4'b0100
  // Clock clock_1: pin names not known; wires that end beside it: phase_1, phase_2, RESET, MANUAL
endmodule

module Decoder (
  input  [3:0] FN,
  input  [3:0] EXEC,
  output [3:0] LDAM,
  output [3:0] LDBM,
  output [3:0] STAM,
  output [3:0] LDAC,
  output [3:0] LDBC,
  output [3:0] LDAP,
  output [3:0] LDAI,
  output [3:0] LDBI,
  output [3:0] STAI,
  output [3:0] BR,
  output [3:0] BRZ,
  output [3:0] BRN,
  output [3:0] BRB,
  output [3:0] ADD,
  output [3:0] SUB,
  output [3:0] PFIX,
  output [3:0] EXEC_2
);

  wire demultiplexer_1_p3, demultiplexer_2_p3, demultiplexer_3_p3, demultiplexer_4_p3, demultiplexer_4_p5,
       demultiplexer_4_p6, demultiplexer_5_p6;

  // Demultiplexer demultiplexer_1: pin names not known; wires that end beside it: LDAM, LDBM, demultiplexer_1_p3, STAM, LDAC
  // Demultiplexer demultiplexer_2: pin names not known; wires that end beside it: STAI, BR, demultiplexer_2_p3, BRZ, BRN
  // Demultiplexer demultiplexer_3: pin names not known; wires that end beside it: LDBC, LDAP, demultiplexer_3_p3, LDAI, LDBI
  // Demultiplexer demultiplexer_4: pin names not known; wires that end beside it: demultiplexer_1_p3, demultiplexer_3_p3, demultiplexer_4_p3, demultiplexer_2_p3, demultiplexer_4_p5, demultiplexer_4_p6
  // Fanout fanout_1: pin names not known; wires that end beside it: EXEC_2, EXEC, demultiplexer_4_p3
  // Demultiplexer demultiplexer_5: pin names not known; wires that end beside it: BRB, ADD, demultiplexer_4_p5, SUB, PFIX, demultiplexer_5_p6
  // Splitter splitter_1: pin names not known; wires that end beside it: demultiplexer_4_p6, demultiplexer_5_p6, FN
endmodule

module Instr_And_Operand_Register (
  input  [3:0] exec,
  input  [3:0] Load_Reg,
  input  [3:0] PFix,
  input  [3:0] RHigh,
  input  [3:0] RLow,
  output [3:0] oreg_highB,
  output [3:0] oreg_highA,
  output [3:0] oreg_lowB,
  output [3:0] oreg_lowA,
  output oreg_high4,
  output oreg_high3,
  output oreg_high1,
  output oreg_high0,
  output oreg_low4,
  output oreg_low3,
  output oreg_low1,
  output oreg_low0,
  output [3:0] toDecode_FN
);

  wire fanout_2_p4, merger_1_p2, register_1_p2, register_1_p3, register_2_p4;

  // Fanout fanout_1: pin names not known; wires that end beside it: {oreg_high4, oreg_high3, oreg_high1, oreg_high0}, oreg_highB, oreg_highA
  // Register register_1: pin names not known; wires that end beside it: {oreg_high4, oreg_high3, oreg_high1, oreg_high0}, register_1_p2, register_1_p3
  // Merger merger_1: pin names not known; wires that end beside it: register_1_p3, merger_1_p2, exec
  // Fanout fanout_2: pin names not known; wires that end beside it: oreg_lowB, oreg_lowA, {oreg_low4, oreg_low3, oreg_low1, oreg_low0}, fanout_2_p4
  // Register register_2: pin names not known; wires that end beside it: merger_1_p2, {oreg_low4, oreg_low3, oreg_low1, oreg_low0}, RLow, register_2_p4
  // Register fn: pin names not known; wires that end beside it: register_2_p4, toDecode_FN, RHigh, Load_Reg
  // Multiplexor multiplexor_1: pin names not known; wires that end beside it: 4'b0000, fanout_2_p4, register_1_p2, PFix
endmodule

module Control (
  input  [3:0] phi1,
  input  [3:0] phi2,
  input  [3:0] FETCH,
  input  [3:0] INCPC,
  input  [3:0] LDAM,
  input  [3:0] LDBM,
  input  [3:0] STAM,
  input  [3:0] LDAC,
  input  [3:0] LDBC,
  input  [3:0] LDAP,
  input  [3:0] LDAI,
  input  [3:0] LDBI,
  input  [3:0] STAI,
  input  [3:0] BR,
  input  [3:0] BRZ,
  input  [3:0] BRN,
  input  [3:0] BRB,
  input  [3:0] ADD,
  input  [3:0] SUB,
  input  [3:0] PFIX,
  input  [3:0] Cond,
  output [3:0] RAMC,
  output [3:0] AUCC,
  output [3:0] AREGC,
  output [3:0] PCC,
  output [3:0] AMUXC,
  output [3:0] BREGC,
  output [3:0] BMUXC,
  output [3:0] PFIX_2,
  output [3:0] LDOREG,
  output [3:0] AUC,
  output [3:0] RMUXC,
  output [3:0] RREGC
);

  wire merger_1_p2, merger_2_p3, merger_2_p4, merger_3_p1, merger_4_p1, merger_5_p3, merger_6_p1,
       merger_7_p3, merger_8_p1, merger_9_p3, merger_9_p4, multiplexor_1_p2, multiplexor_1_p3,
       multiplexor_1_p4, or_1_p4, or_1_p5, or_2_p1, or_2_p2, or_2_p3, or_4_p3, or_6_p6, or_6_p7, or_6_p8,
       or_6_p9, or_6_p10, or_8_p4, or_8_p5, or_9_p3, or_9_p4, or_9_p5, or_9_p6, or_10_p3, or_10_p4, or_11_p6,
       or_11_p7, or_11_p8, or_11_p9, or_11_p10, or_12_p3, or_13_p5, or_13_p6, or_13_p7, or_14_p3, or_15_p6,
       or_15_p7, or_15_p8, or_15_p9, or_15_p10, or_16_p6, or_16_p7, or_16_p8, or_16_p9, or_16_p10, or_17_p2,
       or_18_p3, or_19_p3, or_19_p4, or_19_p5, or_20_p4, or_20_p5, or_21_p5, or_21_p6, or_21_p7, or_22_p5,
       or_22_p6, or_23_p6, or_23_p7, or_23_p8, or_24_p4, or_24_p5, or_24_p6, or_27_p2, or_27_p3, or_27_p4,
       or_28_p3, or_29_p2, or_30_p3, or_31_p2, or_32_p3, or_33_p6, or_34_p6;

  // Merger merger_1: pin names not known; wires that end beside it: phi2, merger_1_p2, RAMC, phi2
  // OR or_1: pin names not known; wires that end beside it: STAM, STAI, merger_1_p2, or_1_p4, or_1_p5
  // OR or_2: pin names not known; wires that end beside it: or_2_p1, or_2_p2, or_2_p3
  // Multiplexor multiplexor_1: pin names not known; wires that end beside it: 4'b0000, multiplexor_1_p2, multiplexor_1_p3, multiplexor_1_p4
  // OR or_3: pin names not known; wires that end beside it: BRZ, BRN, multiplexor_1_p2, or_2_p1
  // Merger merger_2: pin names not known; wires that end beside it: or_2_p2, AUCC, merger_2_p3, merger_2_p4
  // OR or_4: pin names not known; wires that end beside it: or_2_p3, merger_2_p3, or_4_p3
  // OR or_5: pin names not known; wires that end beside it: multiplexor_1_p4, Cond
  // Merger merger_3: pin names not known; wires that end beside it: merger_3_p1, AREGC, phi2
  // OR or_6: pin names not known; wires that end beside it: LDAM, LDAC, LDAP, LDAI, merger_3_p1, or_6_p6, or_6_p7, or_6_p8, or_6_p9, or_6_p10
  // OR or_7: pin names not known; wires that end beside it: or_4_p3, merger_2_p4
  // OR or_8: pin names not known; wires that end beside it: ADD, SUB, or_6_p6, or_8_p4, or_8_p5
  // Merger merger_4: pin names not known; wires that end beside it: merger_4_p1, PCC, phi2
  // OR or_9: pin names not known; wires that end beside it: LDBI, or_1_p4, or_9_p3, or_9_p4, or_9_p5, or_9_p6
  // OR or_10: pin names not known; wires that end beside it: INCPC, merger_4_p1, or_10_p3, or_10_p4
  // OR or_11: pin names not known; wires that end beside it: LDBC, or_6_p8, LDBM, or_6_p7, or_9_p4, or_11_p6, or_11_p7, or_11_p8, or_11_p9, or_11_p10
  // OR or_12: pin names not known; wires that end beside it: or_1_p5, or_11_p6, or_12_p3
  // OR or_13: pin names not known; wires that end beside it: BR, multiplexor_1_p3, BRB, or_10_p3, or_13_p5, or_13_p6, or_13_p7
  // OR or_14: pin names not known; wires that end beside it: or_13_p7, or_12_p3, or_14_p3
  // Merger merger_5: pin names not known; wires that end beside it: or_9_p3, AMUXC, merger_5_p3
  // OR or_15: pin names not known; wires that end beside it: FETCH, or_9_p6, or_6_p9, or_10_p4, merger_5_p3, or_15_p6, or_15_p7, or_15_p8, or_15_p9, or_15_p10
  // OR or_16: pin names not known; wires that end beside it: or_11_p7, or_11_p8, or_11_p9, or_11_p10, or_15_p6, or_16_p6, or_16_p7, or_16_p8, or_16_p9, or_16_p10
  // OR or_17: pin names not known; wires that end beside it: or_16_p6, or_17_p2
  // Merger merger_6: pin names not known; wires that end beside it: merger_6_p1, BREGC, phi2
  // OR or_18: pin names not known; wires that end beside it: or_9_p5, merger_6_p1, or_18_p3
  // OR or_19: pin names not known; wires that end beside it: or_15_p7, or_15_p10, or_19_p3, or_19_p4, or_19_p5
  // OR or_20: pin names not known; wires that end beside it: or_16_p9, or_16_p7, or_18_p3, or_20_p4, or_20_p5
  // OR or_21: pin names not known; wires that end beside it: or_13_p5, or_13_p6, or_14_p3, or_17_p2, or_21_p5, or_21_p6, or_21_p7
  // Merger merger_7: pin names not known; wires that end beside it: or_19_p3, BMUXC, merger_7_p3
  // OR or_22: pin names not known; wires that end beside it: or_15_p8, or_15_p9, or_6_p10, merger_7_p3, or_22_p5, or_22_p6
  // OR or_23: pin names not known; wires that end beside it: or_20_p5, or_16_p8, or_20_p4, or_16_p10, or_22_p5, or_23_p6, or_23_p7, or_23_p8
  // OR or_24: pin names not known; wires that end beside it: or_21_p5, or_21_p6, or_23_p6, or_24_p4, or_24_p5, or_24_p6
  // OR or_25: pin names not known; wires that end beside it: PFIX, PFIX_2
  // Merger merger_8: pin names not known; wires that end beside it: merger_8_p1, LDOREG, phi2
  // OR or_26: pin names not known; wires that end beside it: or_19_p4, merger_8_p1
  // OR or_27: pin names not known; wires that end beside it: or_19_p5, or_27_p2, or_27_p3, or_27_p4
  // OR or_28: pin names not known; wires that end beside it: or_8_p5, or_27_p3, or_28_p3
  // Merger merger_9: pin names not known; wires that end beside it: or_27_p2, AUC, merger_9_p3, merger_9_p4
  // OR or_29: pin names not known; wires that end beside it: merger_9_p3, or_29_p2
  // OR or_30: pin names not known; wires that end beside it: or_28_p3, or_29_p2, or_30_p3
  // OR or_31: pin names not known; wires that end beside it: merger_9_p4, or_31_p2
  // OR or_32: pin names not known; wires that end beside it: or_30_p3, or_31_p2, or_32_p3
  // OR or_33: pin names not known; wires that end beside it: or_22_p6, or_23_p7, or_27_p4, or_23_p8, RMUXC, or_33_p6
  // OR or_34: pin names not known; wires that end beside it: or_24_p4, or_24_p5, or_24_p6, or_21_p7, or_33_p6, or_34_p6
  // OR or_35: pin names not known; wires that end beside it: or_8_p4, or_32_p3, or_34_p6

  assign RREGC = phi1;
endmodule
