// Logisim project CounterMachine_8bitInstructions.circ as structural Verilog: 3 circuits, main circuit main
module main (
);

  wire arithmetic_unit_1_p1, arithmetic_unit_1_p2, demultiplexer_1_p4, demultiplexer_1_p6,
       demultiplexer_2_p2, fanout_1_p3, fanout_2_p2, fanout_2_p4, fanout_3_p3, fanout_4_p1, fanout_4_p5,
       merger_1_p2, merger_2_p1, merger_3_p1, merger_3_p3, merger_3_p4, multiplexor_1_p1, multiplexor_1_p2,
       multiplexor_1_p4, multiplexor_2_p3, multiplexor_2_p5, multiplexor_3_p2, multiplexor_3_p5,
       multiplexor_4_p3, multiplexor_4_p5, or_2_p2, or_2_p3, or_3_p3, or_3_p5, or_3_p6, or_4_p3, or_4_p5,
       or_4_p6, or_4_p7, or_4_p8, or_5_p3, or_6_p3, or_6_p5, ram_2_p1, register_1_p2, right_shift_1_p2,
       right_shift_1_p3, right_shift_2_p3, splitter_1_p1, splitter_1_p3, splitter_2_p1, splitter_2_p2,
       splitter_2_p3;
  wire [3:0] clock_1_p1, clock_1_p2, fanout_4_p2, fanout_4_p3, fanout_4_p6, fanout_5_p2, fanout_5_p3,
       merger_2_p2, merger_4_p3, multiplexor_2_p1, multiplexor_2_p2, multiplexor_3_p4, multiplexor_4_p4,
       register_1_p1, register_1_p3;

  // Splitter splitter_1: pin names not known; wires that end beside it: splitter_1_p1, splitter_1_p1, splitter_1_p3
  // Arithmetic_Unit arithmetic_unit_1: pin names not known; wires that end beside it: arithmetic_unit_1_p1, arithmetic_unit_1_p2
  // Multiplexor multiplexor_1: pin names not known; wires that end beside it: multiplexor_1_p1, multiplexor_1_p2, multiplexor_1_p1, multiplexor_1_p4
  // Multiplexor multiplexor_2: pin names not known; wires that end beside it: multiplexor_2_p1, multiplexor_2_p2, multiplexor_2_p3, multiplexor_2_p3, multiplexor_2_p5
  // Probe on multiplexor_2_p1
  // Probe on multiplexor_2_p2
  RegControl regcontrol_1 (
    .B_MUX(multiplexor_4_p4), .Phase_2(fanout_5_p2), .A_MUX(multiplexor_3_p4), .r0_out(multiplexor_2_p1),
    .r1_out(multiplexor_2_p2), .\input (register_1_p1));
  // Register register_1: pin names not known; wires that end beside it: register_1_p1, register_1_p2, register_1_p3
  // Fanout fanout_1: pin names not known; wires that end beside it: register_1_p2, arithmetic_unit_1_p1, fanout_1_p3
  // Right_Shift right_shift_1: pin names not known; wires that end beside it: arithmetic_unit_1_p2, right_shift_1_p2, right_shift_1_p3
  // Merger merger_1: pin names not known; wires that end beside it: right_shift_1_p3, merger_1_p2
  // Multiplexor multiplexor_3: pin names not known; wires that end beside it: multiplexor_2_p5, multiplexor_3_p2, 4'b0000, multiplexor_3_p4, multiplexor_3_p5
  // Splitter splitter_2: pin names not known; wires that end beside it: splitter_2_p1, splitter_2_p2, splitter_2_p3
  // Fanout fanout_2: pin names not known; wires that end beside it: splitter_2_p2, fanout_2_p2, fanout_2_p2, fanout_2_p4
  // RAM ram_1: pin names not known
  // Multiplexor multiplexor_4: pin names not known; wires that end beside it: multiplexor_3_p5, 4'b0000, multiplexor_4_p3, multiplexor_4_p4, multiplexor_4_p5
  // Fanout fanout_3: pin names not known; wires that end beside it: multiplexor_4_p3, multiplexor_3_p2, fanout_3_p3
  // OR or_1: pin names not known; wires that end beside it: splitter_2_p1, multiplexor_4_p5
  // Right_Shift right_shift_2: pin names not known; wires that end beside it: fanout_2_p4, 4'b0001, right_shift_2_p3
  // Fanout fanout_4: pin names not known; wires that end beside it: fanout_4_p1, fanout_4_p2, fanout_4_p3, fanout_4_p1, fanout_4_p5, fanout_4_p6
  // OR or_2: pin names not known; wires that end beside it: merger_1_p2, or_2_p2, or_2_p3
  // RAM ram_2: pin names not known; wires that end beside it: ram_2_p1, ram_2_p1, multiplexor_1_p2, fanout_1_p3, fanout_4_p5
  // Merger merger_2: pin names not known; wires that end beside it: merger_2_p1, merger_2_p2
  // OR or_3: pin names not known; wires that end beside it: fanout_3_p3, or_2_p3, or_3_p3, or_2_p2, or_3_p5, or_3_p6
  // OR or_4: pin names not known; wires that end beside it: merger_2_p1, or_3_p3, or_4_p3, or_3_p5, or_4_p5, or_4_p6, or_4_p7, or_4_p8
  // Demultiplexer demultiplexer_1: pin names not known; wires that end beside it: right_shift_1_p2, or_4_p3, or_4_p5, demultiplexer_1_p4, or_4_p7, demultiplexer_1_p6
  // Demultiplexer demultiplexer_2: pin names not known; wires that end beside it: demultiplexer_1_p4, demultiplexer_2_p2, 4'b0001, splitter_2_p3
  // Merger merger_3: pin names not known; wires that end beside it: merger_3_p1, merger_3_p1, merger_3_p3, merger_3_p4
  // Merger merger_4: pin names not known; wires that end beside it: or_4_p6, splitter_1_p3, merger_4_p3
  // OR or_5: pin names not known; wires that end beside it: or_3_p6, multiplexor_1_p4, or_5_p3
  // OR or_6: pin names not known; wires that end beside it: or_4_p8, merger_3_p4, or_6_p3, or_5_p3, or_6_p5
  // Demultiplexer demultiplexer_3: pin names not known; wires that end beside it: demultiplexer_1_p6, or_6_p3, or_6_p5, demultiplexer_2_p2, right_shift_2_p3
  // Fanout fanout_5: pin names not known; wires that end beside it: merger_3_p3, fanout_5_p2, fanout_5_p3
  PC pc_1 (
    .low4(fanout_4_p2), .high4(fanout_4_p3), .phase1Out(register_1_p3), .phase2Out(fanout_5_p3),
    .jumpADR(fanout_4_p6), .phase1(clock_1_p1), .phase2(clock_1_p2), .muxControl(merger_4_p3),
    .AUControl(merger_2_p2));
  Button button_1 ();  // open: out
  // Clock clock_1: pin names not known; wires that end beside it: clock_1_p1, clock_1_p2
  Button button_2 ();  // open: out

  // Notes on the sheet:
  //   a
  //   2lsb
  //   DATA MEMORY
  //   STR
  //   LDR
  //   000x 0000 - INC
  //   001x 0000 - DEC
  //   0100 a3a2a1a0 - JNZ
  //   100x a3a2a1a0 - STR
  //   101x a3a2a1a0 - LDR
endmodule

module RegControl (
  input  [3:0] B_MUX,
  input  [3:0] Phase_2,
  input  [3:0] A_MUX,
  input  [3:0] \input ,
  output [3:0] r0_out,
  output [3:0] r1_out
);

  wire fanout_1_p3, merger_1_p3, R0_p2, R0_p3, R0_p4;

  // Register R0: pin names not known; wires that end beside it: r0_out, R0_p2, R0_p3, R0_p4
  // Merger merger_1: pin names not known; wires that end beside it: B_MUX, R0_p3, merger_1_p3
  // Fanout fanout_1: pin names not known; wires that end beside it: R0_p4, \input , fanout_1_p3
  // Register R1: pin names not known; wires that end beside it: r1_out, merger_1_p3, fanout_1_p3
  // Merger merger_2: pin names not known; wires that end beside it: R0_p2, Phase_2, A_MUX
endmodule

module PC (
  input  [3:0] phase1,
  input  [3:0] phase2,
  input  [3:0] muxControl,
  input  [3:0] AUControl,
  input  [3:0] jumpADR,
  output [3:0] low4,
  output [3:0] high4,
  output [3:0] phase1Out,
  output [3:0] phase2Out
);

  wire fanout_1_p1, fanout_2_p3, fanout_3_p1, fanout_4_p3, multiplexor_1_p1, multiplexor_1_p2,
       multiplexor_1_p4, multiplexor_1_p5, multiplexor_2_p2, multiplexor_2_p3, multiplexor_2_p5,
       register_1_p2, register_2_p2, register_2_p3, register_4_p2;

  // Fanout fanout_1: pin names not known; wires that end beside it: fanout_1_p1, high4
  // Register register_1: pin names not known; wires that end beside it: phase1Out, register_1_p2
  // Register register_2: pin names not known; wires that end beside it: phase2Out, register_2_p2, register_2_p3
  // Multiplexor multiplexor_1: pin names not known; wires that end beside it: multiplexor_1_p1, multiplexor_1_p2, register_2_p2, multiplexor_1_p4, multiplexor_1_p5
  // Fanout fanout_2: pin names not known; wires that end beside it: multiplexor_1_p1, multiplexor_1_p2, fanout_2_p3, fanout_2_p3, multiplexor_1_p4
  // Arithmetic_Unit arithmetic_unit_1: pin names not known; wires that end beside it: fanout_1_p1
  // Fanout fanout_3: pin names not known; wires that end beside it: fanout_3_p1, low4
  // Register register_3: pin names not known; wires that end beside it: register_1_p2, phase1
  // Register register_4: pin names not known; wires that end beside it: register_2_p3, register_4_p2, register_4_p2, phase2
  // Multiplexor multiplexor_2: pin names not known; wires that end beside it: multiplexor_1_p5, multiplexor_2_p2, multiplexor_2_p3, jumpADR, multiplexor_2_p5, muxControl
  // Fanout fanout_4: pin names not known; wires that end beside it: multiplexor_2_p2, multiplexor_2_p3, fanout_4_p3, fanout_4_p3, multiplexor_2_p5
  // Arithmetic_Unit arithmetic_unit_2: pin names not known; wires that end beside it: fanout_3_p1, AUControl
endmodule
