// Logisim project PedestrianTrafficLights.circ as structural Verilog: 5 circuits, main circuit main
module main (
);

  wire clk_1_phi_1, clk_1_phi_2, delta_1_q0_prime, delta_1_q1_prime, nandlatch_1_out, nandlatch_2_out,
       nandlatch_3_out, nandlatch_4_out, omega_1_a, omega_1_g, omega_1_r, PEDESTRIAN_out, RST_out;

  clk clk_1 (.phi_1(clk_1_phi_1), .phi_2(clk_1_phi_2));
  Button RST (.out(RST_out));
  Button PEDESTRIAN (.out(PEDESTRIAN_out));
  NANDLatch nandlatch_1 (.D(delta_1_q0_prime), .CLK(clk_1_phi_1), .OUT(nandlatch_1_out));
  NANDLatch nandlatch_2 (.D(nandlatch_1_out), .CLK(clk_1_phi_2), .OUT(nandlatch_2_out));
  NANDLatch nandlatch_3 (.D(delta_1_q1_prime), .CLK(clk_1_phi_1), .OUT(nandlatch_3_out));
  Delta delta_1 (
    .rst(RST_out), .Pedestrian(PEDESTRIAN_out), .Q0(nandlatch_2_out), .Q1(nandlatch_4_out),
    .Q0_prime(delta_1_q0_prime), .Q1_prime(delta_1_q1_prime));
  NANDLatch nandlatch_4 (.D(nandlatch_3_out), .CLK(clk_1_phi_2), .OUT(nandlatch_4_out));
  Omega omega_1 (.Q0(nandlatch_2_out), .Q1(nandlatch_4_out), .R(omega_1_r), .A(omega_1_a), .G(omega_1_g));
  LED led_1 (.in(omega_1_r));
  LED led_2 (.in(omega_1_a));
  LED led_3 (.in(omega_1_g));
endmodule

module clk (
  output phi_1,
  output phi_2
);

  wire clock_1_out, nand_1_out, nand_2_out, not_1_out, not_2_out, not_3_out;

  Clock clock_1 (.out(clock_1_out));
  not not_1 (not_1_out, clock_1_out);
  not not_2 (not_2_out, nand_1_out);
  nand nand_1 (nand_1_out, not_1_out, phi_2);
  nand nand_2 (nand_2_out, phi_1, clock_1_out);
  not not_3 (not_3_out, nand_2_out);
  not not_4 (phi_1, not_2_out);
  not not_5 (phi_2, not_3_out);
endmodule

module NANDLatch (
  input  D,
  input  CLK,
  output OUT
);

  wire nand_1_out, nand_2_out, nand_4_out;

  nand nand_1 (nand_1_out, D, CLK);
  nand nand_2 (nand_2_out, nand_1_out, CLK);
  nand nand_3 (OUT, nand_1_out, nand_4_out);
  nand nand_4 (nand_4_out, OUT, nand_2_out);
endmodule

module Delta (
  input  rst,
  input  Pedestrian,
  input  Q0,
  input  Q1,
  output Q0_prime,
  output Q1_prime
);

  wire and_1_out, and_2_out, and_3_out, and_4_out;

  and and_1 (and_1_out, ~Q0, Q1, ~rst);  // AND_Gate
  or or_1 (Q0_prime, and_1_out, and_2_out);
  and and_2 (and_2_out, Q0, ~Q1, ~rst);  // AND_Gate
  and and_3 (and_3_out, ~rst, ~Pedestrian, ~Q0, ~Q1);  // AND_Gate
  or or_2 (Q1_prime, and_3_out, and_4_out);
  and and_4 (and_4_out, ~rst, Pedestrian, Q0, ~Q1);  // AND_Gate
endmodule

module Omega (
  input  Q0,
  input  Q1,
  output R,
  output A,
  output G
);

  not not_1 (R, Q0);
  and and_1 (G, Q0, ~Q1);  // AND_Gate

  assign A = Q1;
endmodule
