// Logisim project CounterMachine.circ as structural Verilog: 1 circuit, main circuit main
module main (
  input  [3:0] in_1,
  input  [3:0] in_2,
  input  [3:0] in_3,
  input  [3:0] in_4
);

  wire arithmetic_unit_1_p1, arithmetic_unit_1_p2, arithmetic_unit_1_p3, fanout_1_p2, fanout_1_p3,
       fanout_2_p4, fanout_3_p2, fanout_3_p3, fanout_4_p1, fanout_4_p3, fanout_5_p3, merger_1_p1,
       merger_1_p2, merger_1_p3, merger_2_p1, merger_2_p3, merger_3_p2, merger_4_p1, merger_4_p2,
       merger_5_p3, multiplexor_1_p1, multiplexor_1_p2, multiplexor_1_p4, multiplexor_3_p2, multiplexor_3_p5,
       multiplexor_4_p3, multiplexor_4_p5, multiplexor_6_p1, multiplexor_6_p2, multiplexor_6_p4, or_1_p2,
       or_1_p3, or_2_p3, or_2_p5, or_2_p6, or_2_p7, R0_p3, R0_p4, ram_1_p2, register_1_p3, register_2_p3,
       register_2_p4, register_3_p3, register_3_p5, right_shift_1_p2, right_shift_1_p3, splitter_1_p1,
       splitter_1_p3, splitter_2_p1, splitter_2_p2, splitter_2_p3, splitter_2_p4;

  // Splitter splitter_1: pin names not known; wires that end beside it: splitter_1_p1, splitter_1_p1, splitter_1_p3
  // Arithmetic_Unit arithmetic_unit_1: pin names not known; wires that end beside it: arithmetic_unit_1_p1, arithmetic_unit_1_p2, arithmetic_unit_1_p3
  // Multiplexor multiplexor_1: pin names not known; wires that end beside it: multiplexor_1_p1, multiplexor_1_p2, arithmetic_unit_1_p1, multiplexor_1_p4
  // Merger merger_1: pin names not known; wires that end beside it: merger_1_p1, merger_1_p2, merger_1_p3
  // Register R0: pin names not known; wires that end beside it: multiplexor_1_p1, merger_1_p1, R0_p3, R0_p4
  // Merger merger_2: pin names not known; wires that end beside it: merger_2_p1, R0_p3, merger_2_p3
  // Fanout fanout_1: pin names not known; wires that end beside it: R0_p4, fanout_1_p2, fanout_1_p3
  // Register register_1: pin names not known; wires that end beside it: fanout_1_p2, arithmetic_unit_1_p2, register_1_p3
  // Register R1: pin names not known; wires that end beside it: multiplexor_1_p2, merger_2_p3, fanout_1_p3
  // Multiplexor multiplexor_2: pin names not known; wires that end beside it: in_1, in_2, in_3, in_4
  // Multiplexor multiplexor_3: pin names not known; wires that end beside it: multiplexor_1_p4, multiplexor_3_p2, 4'b0000, merger_1_p3, multiplexor_3_p5
  // Right_Shift right_shift_1: pin names not known; wires that end beside it: arithmetic_unit_1_p3, right_shift_1_p2, right_shift_1_p3
  // Merger merger_3: pin names not known; wires that end beside it: right_shift_1_p3, merger_3_p2
  // Splitter splitter_2: pin names not known; wires that end beside it: splitter_2_p1, splitter_2_p2, splitter_2_p3, splitter_2_p4
  // RAM ram_1: pin names not known; wires that end beside it: splitter_2_p2, ram_1_p2
  // Multiplexor multiplexor_4: pin names not known; wires that end beside it: multiplexor_3_p5, 4'b0000, multiplexor_4_p3, merger_2_p1, multiplexor_4_p5
  // Fanout fanout_2: pin names not known; wires that end beside it: multiplexor_4_p3, multiplexor_3_p2, merger_3_p2, fanout_2_p4
  // Fanout fanout_3: pin names not known; wires that end beside it: splitter_2_p1, fanout_3_p2, fanout_3_p3
  // Merger merger_4: pin names not known; wires that end beside it: merger_4_p1, merger_4_p2
  // OR or_1: pin names not known; wires that end beside it: fanout_2_p4, or_1_p2, or_1_p3
  // OR or_2: pin names not known; wires that end beside it: merger_4_p1, or_1_p2, or_2_p3, or_1_p3, or_2_p5, or_2_p6, or_2_p7
  // Demultiplexer demultiplexer_1: pin names not known; wires that end beside it: right_shift_1_p2, or_2_p3, or_2_p5, 4'b0001, or_2_p7, splitter_2_p3
  // Multiplexor multiplexor_5: pin names not known; wires that end beside it: fanout_3_p2, 4'b0000, multiplexor_4_p5, splitter_2_p4
  // Merger merger_5: pin names not known; wires that end beside it: or_2_p6, splitter_1_p3, merger_5_p3
  // Fanout fanout_4: pin names not known; wires that end beside it: fanout_4_p1, ram_1_p2, fanout_4_p3
  // Register register_2: pin names not known; wires that end beside it: register_1_p3, fanout_4_p3, register_2_p3, register_2_p4
  // Register register_3: pin names not known; wires that end beside it: merger_1_p2, register_2_p3, register_3_p3, register_3_p3, register_3_p5
  // Multiplexor multiplexor_6: pin names not known; wires that end beside it: multiplexor_6_p1, multiplexor_6_p2, fanout_3_p3, multiplexor_6_p4, merger_5_p3
  // Fanout fanout_5: pin names not known; wires that end beside it: multiplexor_6_p1, multiplexor_6_p2, fanout_5_p3, fanout_5_p3, multiplexor_6_p4
  // Arithmetic_Unit arithmetic_unit_2: pin names not known; wires that end beside it: fanout_4_p1, merger_4_p2
  Button button_1 ();  // open: out
  // Clock clock_1: pin names not known; wires that end beside it: register_2_p4, register_3_p5
  Button button_2 ();  // open: out

  // Notes on the sheet:
  //   00xx - ADD
  //   01xx - SUB
  //   10xx - JNZ
  //   1100 - HALT
endmodule
