// Logisim project CounterMachineDECODER.circ as structural Verilog: 2 circuits, main circuit main
module main (
  input  [3:0] in_1,
  input  [3:0] in_2,
  input  [3:0] in_3,
  input  [3:0] in_4
);

  wire arithmetic_unit_1_p2, arithmetic_unit_1_p3, fanout_1_p2, fanout_1_p3, fanout_2_p1, fanout_2_p3,
       fanout_3_p3, merger_1_p1, merger_1_p2, merger_2_p3, multiplexor_1_p1, multiplexor_1_p2,
       multiplexor_3_p1, multiplexor_3_p2, multiplexor_3_p4, R0_p3, R0_p4, ram_1_p2, register_1_p3,
       register_2_p3, register_2_p4, register_3_p3, register_3_p5;
  wire [3:0] arithmetic_unit_1_p1, arithmetic_unit_1_p4, decoder_1_muxpccontrol, decoder_1_muxpcinput,
       decoder_1_pc_au, merger_1_p3, merger_2_p1, multiplexor_1_p4, ram_1_p1;

  // Arithmetic_Unit arithmetic_unit_1: pin names not known; wires that end beside it: arithmetic_unit_1_p1, arithmetic_unit_1_p2, arithmetic_unit_1_p3, arithmetic_unit_1_p4
  // Multiplexor multiplexor_1: pin names not known; wires that end beside it: multiplexor_1_p1, multiplexor_1_p2, arithmetic_unit_1_p2, multiplexor_1_p4
  // Merger merger_1: pin names not known; wires that end beside it: merger_1_p1, merger_1_p2, merger_1_p3
  // Register R0: pin names not known; wires that end beside it: multiplexor_1_p1, merger_1_p1, R0_p3, R0_p4
  // Merger merger_2: pin names not known; wires that end beside it: merger_2_p1, R0_p3, merger_2_p3
  // Fanout fanout_1: pin names not known; wires that end beside it: R0_p4, fanout_1_p2, fanout_1_p3
  // Register register_1: pin names not known; wires that end beside it: fanout_1_p2, arithmetic_unit_1_p3, register_1_p3
  // Register R1: pin names not known; wires that end beside it: multiplexor_1_p2, merger_2_p3, fanout_1_p3
  // Multiplexor multiplexor_2: pin names not known; wires that end beside it: in_1, in_2, in_3, in_4
  // RAM ram_1: pin names not known; wires that end beside it: ram_1_p1, ram_1_p2
  DECODER decoder_1 (
    .BOOL_TEST(arithmetic_unit_1_p1), .muxAU(multiplexor_1_p4), .AU(arithmetic_unit_1_p4),
    .muxPCcontrol(decoder_1_muxpccontrol), .muxPCinput(decoder_1_muxpcinput), .MERGER0(merger_1_p3),
    .MERGER1(merger_2_p1), .PC_AU(decoder_1_pc_au), .INSTRUCTION(ram_1_p1));
  // Fanout fanout_2: pin names not known; wires that end beside it: fanout_2_p1, ram_1_p2, fanout_2_p3
  // Register register_2: pin names not known; wires that end beside it: register_1_p3, fanout_2_p3, register_2_p3, register_2_p4
  // Register register_3: pin names not known; wires that end beside it: merger_1_p2, register_2_p3, register_3_p3, register_3_p3, register_3_p5
  // Multiplexor multiplexor_3: pin names not known; wires that end beside it: multiplexor_3_p1, multiplexor_3_p2, decoder_1_muxpcinput, multiplexor_3_p4, decoder_1_muxpccontrol
  // Fanout fanout_3: pin names not known; wires that end beside it: multiplexor_3_p1, multiplexor_3_p2, fanout_3_p3, fanout_3_p3, multiplexor_3_p4
  // Arithmetic_Unit arithmetic_unit_2: pin names not known; wires that end beside it: fanout_2_p1, decoder_1_pc_au
  // Clock clock_1: pin names not known; wires that end beside it: register_2_p4, register_3_p5
  Button button_1 ();  // open: out
  Button button_2 ();  // open: out

  // Notes on the sheet:
  //   00xx - INC
  //   01xx - DEC
  //   10xx - JNZ
  //   1100 - HALT
endmodule

module DECODER (
  input  [3:0] BOOL_TEST,
  input  [3:0] INSTRUCTION,
  output [3:0] muxPCcontrol,
  output [3:0] PC_AU,
  output [3:0] MERGER0,
  output [3:0] MERGER1,
  output [3:0] muxAU,
  output [3:0] AU,
  output [3:0] muxPCinput
);

  wire fanout_1_p4, fanout_2_p2, merger_1_p2, merger_2_p1, multiplexor_1_p2, multiplexor_1_p5,
       multiplexor_2_p3, multiplexor_2_p5, or_1_p2, or_1_p3, or_2_p3, or_2_p5, or_2_p6, or_2_p7,
       right_shift_1_p2, right_shift_1_p3, splitter_1_p1, splitter_1_p3, splitter_1_p4, splitter_2_p2;

  // Multiplexor multiplexor_1: pin names not known; wires that end beside it: muxAU, multiplexor_1_p2, 4'b0000, MERGER0, multiplexor_1_p5
  // Right_Shift right_shift_1: pin names not known; wires that end beside it: AU, right_shift_1_p2, right_shift_1_p3
  // Merger merger_1: pin names not known; wires that end beside it: right_shift_1_p3, merger_1_p2
  // Splitter splitter_1: pin names not known; wires that end beside it: splitter_1_p1, INSTRUCTION, splitter_1_p3, splitter_1_p4
  // Multiplexor multiplexor_2: pin names not known; wires that end beside it: multiplexor_1_p5, 4'b0000, multiplexor_2_p3, MERGER1, multiplexor_2_p5
  // Fanout fanout_1: pin names not known; wires that end beside it: multiplexor_2_p3, multiplexor_1_p2, merger_1_p2, fanout_1_p4
  // Fanout fanout_2: pin names not known; wires that end beside it: splitter_1_p1, fanout_2_p2, muxPCinput
  // Splitter splitter_2: pin names not known; wires that end beside it: BOOL_TEST, splitter_2_p2
  // Merger merger_2: pin names not known; wires that end beside it: merger_2_p1, PC_AU
  // OR or_1: pin names not known; wires that end beside it: fanout_1_p4, or_1_p2, or_1_p3
  // OR or_2: pin names not known; wires that end beside it: merger_2_p1, or_1_p2, or_2_p3, or_1_p3, or_2_p5, or_2_p6, or_2_p7
  // Demultiplexer demultiplexer_1: pin names not known; wires that end beside it: right_shift_1_p2, or_2_p3, or_2_p5, 4'b0001, or_2_p7, splitter_1_p3
  // Multiplexor multiplexor_3: pin names not known; wires that end beside it: fanout_2_p2, 4'b0000, multiplexor_2_p5, splitter_1_p4
  // Merger merger_3: pin names not known; wires that end beside it: or_2_p6, splitter_2_p2, muxPCcontrol

  // Notes on the sheet:
  //   2 lsb
  //   2 msb
  //   1 msb
endmodule
