// Logisim project AND_NOR.circ as structural Verilog: 4 circuits, main circuit main
module main (
  input  in_1,
  input  in_2,
  output out_3
);

  wire mynor_1_x, mynor_2_x;

  myNOR mynor_1 (.a(in_1), .b(in_1), .x(mynor_1_x));
  myNOR mynor_2 (.a(in_2), .b(in_2), .x(mynor_2_x));
  myNOR mynor_3 (.a(mynor_1_x), .b(mynor_2_x), .x(out_3));
endmodule

module myNAND (
  input  x,
  input  y,
  output r
);

  wire not_1_out, not_2_out;

  not not_1 (not_1_out, x);
  not not_2 (not_2_out, y);
  or or_1 (r, not_1_out, not_2_out);
endmodule

// NOR
module myNOR (
  input  a,
  input  b,
  output x
);

  wire not_1_out, not_2_out;

  not not_1 (not_1_out, a);
  not not_2 (not_2_out, b);
  and and_1 (x, not_1_out, not_2_out);
endmodule

module myNOT (
  input  x,
  output r
);

  not not_1 (r, x);
endmodule
