// Logisim project NAND.circ as structural Verilog: 1 circuit, main circuit main
module main (
  input  x,
  input  y,
  output r
);

  wire transistor_4_out;

  Transistor transistor_1 (.in(1'b1), .out(r), .gate(x));
  Transistor transistor_2 (.in(1'b1), .out(r), .gate(y));
  Transistor #(.\type ("n")) transistor_3 (.in(transistor_4_out), .out(r), .gate(x));
  Transistor #(.\type ("n")) transistor_4 (.in(1'b0), .out(transistor_4_out), .gate(y));
endmodule
