// Logisim project NOT.circ as structural Verilog: 1 circuit, main circuit main
module main (
  input  x,
  output r
);

  Transistor transistor_1 (.in(1'b1), .out(r), .gate(x));
  Transistor #(.\type ("n")) transistor_2 (.in(1'b0), .out(r), .gate(x));
endmodule
