// Logisim project OR_NAND.circ as structural Verilog: 4 circuits, main circuit main
module main (
  input  in_1,
  input  in_2,
  output out_3
);

  wire mynand_1_r, mynand_2_r;

  myNAND mynand_1 (.x(in_1), .y(in_1), .r(mynand_1_r));
  myNAND mynand_2 (.x(in_2), .y(in_2), .r(mynand_2_r));
  myNAND mynand_3 (.x(mynand_1_r), .y(mynand_2_r), .r(out_3));
endmodule

module myNAND (
  input  x,
  input  y,
  output r
);

  wire not_1_out, not_2_out;

  not not_1 (not_1_out, x);
  not not_2 (not_2_out, y);
  or or_1 (r, not_1_out, not_2_out);
endmodule

module myNOR (
  input  a,
  input  b,
  output x
);

  wire not_1_out, not_2_out;

  not not_1 (not_1_out, a);
  not not_2 (not_2_out, b);
  and and_1 (x, not_1_out, not_2_out);
endmodule

module myNOT (
  input  x,
  output r
);

  not not_1 (r, x);
endmodule
