// Logisim project q4d.circ as structural Verilog: 1 circuit, main circuit main
module main (
  input  in_1,
  input  in_2,
  input  in_3,
  output out_4
);

  wire transistor_5_out, transistor_6_out;

  Transistor transistor_1 (.in(1'b1), .out(out_4), .gate(in_1));
  Transistor transistor_2 (.in(1'b1), .out(out_4), .gate(in_2));
  Transistor transistor_3 (.in(1'b1), .out(out_4), .gate(in_3));
  Transistor #(.\type ("n")) transistor_4 (.in(transistor_5_out), .out(out_4), .gate(in_1));
  Transistor #(.\type ("n")) transistor_5 (.in(transistor_6_out), .out(transistor_5_out), .gate(in_2));
  Transistor #(.\type ("n")) transistor_6 (.in(1'b0), .out(transistor_6_out), .gate(in_3));
endmodule
