// Logisim project Q3a.circ as structural Verilog: 2 circuits, main circuit 4bitFUlladder
module _4bitFUlladder (
  input  in_1,
  input  in_2,
  input  in_3,
  input  in_4,
  input  in_5,
  input  in_6,
  input  in_7,
  input  in_8,
  input  in_9,
  output out_10,
  output out_11,
  output out_12,
  output out_13,
  output out_14
);

  wire fulladder_2_out_5, fulladder_3_out_5, fulladder_4_out_5;

  FullAdder fulladder_1 (.in_1(in_1), .in_2(in_6), .in_3(fulladder_2_out_5), .out_4(out_11), .out_5(out_10));
  FullAdder fulladder_2 (.in_1(in_2), .in_2(in_7), .in_3(fulladder_3_out_5), .out_4(out_12), .out_5(fulladder_2_out_5));
  FullAdder fulladder_3 (.in_1(in_3), .in_2(in_8), .in_3(fulladder_4_out_5), .out_4(out_13), .out_5(fulladder_3_out_5));
  FullAdder fulladder_4 (.in_1(in_4), .in_2(in_9), .in_3(in_5), .out_4(out_14), .out_5(fulladder_4_out_5));
endmodule

module FullAdder (
  input  in_1,
  input  in_2,
  input  in_3,
  output out_4,
  output out_5
);

  wire nand_1_out, nand_2_out, nand_3_out, nand_4_out, nand_5_out, nand_6_out, nand_7_out;

  nand nand_1 (nand_1_out, in_1, in_2);
  nand nand_2 (nand_2_out, in_1, nand_1_out);
  nand nand_3 (nand_3_out, nand_1_out, in_2);
  nand nand_4 (nand_4_out, nand_2_out, nand_3_out);
  nand nand_5 (nand_5_out, nand_4_out, in_3);
  nand nand_6 (nand_6_out, nand_4_out, nand_5_out);
  nand nand_7 (nand_7_out, nand_5_out, in_3);
  nand nand_8 (out_4, nand_6_out, nand_7_out);
  nand Cout (out_5, nand_5_out, nand_1_out);
endmodule
