// Logisim project Q2.circ as structural Verilog: 3 circuits, main circuit main
module main (
  input  in_1,
  output out_2,
  output out_3,
  output out_4,
  output out_5
);

  wire adder_1_cout, adder_1_out, adder_2_cout, adder_2_out, adder_3_cout, adder_3_out, adder_4_out,
       and_1_out, and_2_out, and_3_out, and_4_out, clk_2phase_1_phi_1, clk_2phase_1_phi_2,
       dlatchnand_1_out_3, dlatchnand_3_out_3, dlatchnand_5_out_3, dlatchnand_7_out_3, not_1_out;

  clk_2phase clk_2phase_1 (.phi_1(clk_2phase_1_phi_1), .phi_2(clk_2phase_1_phi_2));
  not not_1 (not_1_out, in_1);
  DLatchNAND dlatchnand_1 (.in_1(and_1_out), .in_2(clk_2phase_1_phi_1), .out_3(dlatchnand_1_out_3));  // open: out_4
  and and_1 (and_1_out, not_1_out, adder_1_out);
  DLatchNAND dlatchnand_2 (.in_1(dlatchnand_1_out_3), .in_2(clk_2phase_1_phi_2), .out_3(out_2));  // open: out_4
  Adder #(.width(1)) adder_1 (.a(out_2), .b(1'b1), .out(adder_1_out), .cin(1'b0), .cout(adder_1_cout));
  DLatchNAND dlatchnand_3 (.in_1(and_2_out), .in_2(clk_2phase_1_phi_1), .out_3(dlatchnand_3_out_3));  // open: out_4
  and and_2 (and_2_out, not_1_out, adder_2_out);
  Adder #(.width(1)) adder_2 (.a(out_3), .b(1'b0), .out(adder_2_out), .cin(adder_1_cout), .cout(adder_2_cout));
  DLatchNAND dlatchnand_4 (.in_1(dlatchnand_3_out_3), .in_2(clk_2phase_1_phi_2), .out_3(out_3));  // open: out_4
  DLatchNAND dlatchnand_5 (.in_1(and_3_out), .in_2(clk_2phase_1_phi_1), .out_3(dlatchnand_5_out_3));  // open: out_4
  and and_3 (and_3_out, not_1_out, adder_3_out);
  Adder #(.width(1)) adder_3 (.a(out_4), .b(1'b0), .out(adder_3_out), .cin(adder_2_cout), .cout(adder_3_cout));
  DLatchNAND dlatchnand_6 (.in_1(dlatchnand_5_out_3), .in_2(clk_2phase_1_phi_2), .out_3(out_4));  // open: out_4
  DLatchNAND dlatchnand_7 (.in_1(and_4_out), .in_2(clk_2phase_1_phi_1), .out_3(dlatchnand_7_out_3));  // open: out_4
  and and_4 (and_4_out, not_1_out, adder_4_out);
  Adder #(.width(1)) adder_4 (.a(out_5), .b(1'b0), .out(adder_4_out), .cin(adder_3_cout));  // open: cout
  DLatchNAND dlatchnand_8 (.in_1(dlatchnand_7_out_3), .in_2(clk_2phase_1_phi_2), .out_3(out_5));  // open: out_4
endmodule

module clk_2phase (
  output phi_1,
  output phi_2
);

  wire clock_1_out, nand_1_out, nand_2_out, not_1_out, not_2_out, not_3_out;

  Clock clock_1 (.out(clock_1_out));
  not not_1 (not_1_out, clock_1_out);
  not not_2 (not_2_out, nand_1_out);
  nand nand_1 (nand_1_out, not_1_out, phi_2);
  nand nand_2 (nand_2_out, phi_1, clock_1_out);
  not not_3 (not_3_out, nand_2_out);
  not not_4 (phi_1, not_2_out);
  not not_5 (phi_2, not_3_out);
endmodule

module DLatchNAND (
  input  in_1,
  input  in_2,
  output out_3,
  output out_4
);

  wire nand_1_out, nand_2_out;

  nand nand_1 (nand_1_out, in_1, in_2);
  nand nand_2 (nand_2_out, in_2, nand_1_out);
  nand nand_3 (out_3, nand_1_out, out_4);
  nand nand_4 (out_4, out_3, nand_2_out);
endmodule
