// Logisim project traffic.circ as structural Verilog
module main (
);

  wire clk_1_phi_1, clk_1_phi_2, delta_1_q0_prime, delta_1_q1_prime, delta_1_q2_prime, dlatchnand_1_q,
       dlatchnand_2_q, dlatchnand_3_q, dlatchnand_4_q, dlatchnand_5_q, dlatchnand_6_q, omega_1_aa,
       omega_1_ag, omega_1_ar, omega_1_ma, omega_1_mg, omega_1_mr, RST_out;

  clk clk_1 (.phi_1(clk_1_phi_1), .phi_2(clk_1_phi_2));
  Button RST (.out(RST_out));
  DLatchNAND dlatchnand_1 (.in_1(delta_1_q0_prime), .CLK(clk_1_phi_1), .Q(dlatchnand_1_q));
  DLatchNAND dlatchnand_2 (.in_1(dlatchnand_1_q), .CLK(clk_1_phi_2), .Q(dlatchnand_2_q));
  DLatchNAND dlatchnand_3 (.in_1(delta_1_q1_prime), .CLK(clk_1_phi_1), .Q(dlatchnand_3_q));
  Delta delta_1 (
    .RST(RST_out), .Q0(dlatchnand_2_q), .Q1(dlatchnand_4_q), .Q2(dlatchnand_6_q),
    .Q0_prime(delta_1_q0_prime), .Q1_prime(delta_1_q1_prime), .Q2_prime(delta_1_q2_prime));
  DLatchNAND dlatchnand_4 (.in_1(dlatchnand_3_q), .CLK(clk_1_phi_2), .Q(dlatchnand_4_q));
  DLatchNAND dlatchnand_5 (.in_1(delta_1_q2_prime), .CLK(clk_1_phi_1), .Q(dlatchnand_5_q));
  DLatchNAND dlatchnand_6 (.in_1(dlatchnand_5_q), .CLK(clk_1_phi_2), .Q(dlatchnand_6_q));
  LED led_1 (.in(omega_1_mr));
  LED led_2 (.in(omega_1_ma));
  Omega omega_1 (
    .Q0(dlatchnand_2_q), .Q1(dlatchnand_4_q), .Q2(dlatchnand_6_q), .Mr(omega_1_mr), .Ma(omega_1_ma),
    .Mg(omega_1_mg), .Ar(omega_1_ar), .Aa(omega_1_aa), .Ag(omega_1_ag));
  LED led_3 (.in(omega_1_mg));
  LED led_4 (.in(omega_1_ar));
  LED led_5 (.in(omega_1_aa));
  LED led_6 (.in(omega_1_ag));

  // Notes on the sheet:
  //   MAIN
  //   ACCESS
endmodule

module clk (
  output phi_1,
  output phi_2
);

  wire clock_1_out, nand_1_out, nand_2_out, not_1_out, not_2_out, not_3_out;

  Clock clock_1 (.out(clock_1_out));
  not not_1 (not_1_out, clock_1_out);
  not not_2 (not_2_out, nand_1_out);
  nand nand_1 (nand_1_out, not_1_out, phi_2);
  not not_3 (not_3_out, nand_2_out);
  nand nand_2 (nand_2_out, phi_1, clock_1_out);
  not not_4 (phi_1, not_2_out);
  not not_5 (phi_2, not_3_out);
endmodule

module Delta (
  input  RST,
  input  Q0,
  input  Q1,
  input  Q2,
  output Q0_prime,
  output Q1_prime,
  output Q2_prime
);

  wire and_1_out, and_2_out, and_3_out, and_4_out, and_5_out, and_6_out, not_1_out, not_2_out, not_3_out,
       not_4_out;

  not not_1 (not_1_out, RST);
  not not_2 (not_2_out, Q0);
  not not_3 (not_3_out, Q1);
  not not_4 (not_4_out, Q2);
  and and_1 (and_1_out, Q0, Q1);
  and and_2 (and_2_out, not_1_out, not_2_out, not_4_out);
  and and_3 (and_3_out, not_2_out, not_3_out, not_1_out);
  and and_4 (and_4_out, not_4_out, not_3_out, Q0);
  and and_5 (and_5_out, not_4_out, Q1, not_2_out);
  and and_6 (and_6_out, not_3_out, not_2_out, Q2);
  or or_1 (Q0_prime, and_2_out, and_3_out);
  or or_2 (Q1_prime, RST, and_4_out, and_5_out);
  or or_3 (Q2_prime, RST, and_1_out, and_6_out);
endmodule

module Omega (
  input  Q0,
  input  Q1,
  input  Q2,
  output Mr,
  output Ma,
  output Mg,
  output Ar,
  output Aa,
  output Ag
);

  wire and_1_out, and_2_out, and_5_out, and_6_out, and_8_out, not_1_out, not_2_out, not_3_out;

  not not_1 (not_1_out, Q0);
  not not_2 (not_2_out, Q1);
  not not_3 (not_3_out, Q2);
  and and_1 (and_1_out, not_3_out, Q1, not_1_out);
  and and_2 (and_2_out, not_1_out, Q2);
  or or_1 (Mr, and_2_out, Q1);
  and and_3 (Ma, Q0, not_2_out);
  and and_4 (Mg, not_1_out, not_2_out, not_3_out);
  and and_5 (and_5_out, not_3_out, not_2_out);
  and and_6 (and_6_out, Q2, Q1);
  and and_7 (Ag, Q1, Q0);
  or or_2 (Ar, Ma, and_5_out, and_6_out);
  and and_8 (and_8_out, not_1_out, not_2_out, Q2);
  or or_3 (Aa, and_1_out, and_8_out);
endmodule

module DLatchNAND (
  input  in_1,
  input  CLK,
  output Q
);

  wire nand_1_out, nand_2_out, nand_4_out;

  nand nand_1 (nand_1_out, in_1, CLK);
  nand nand_2 (nand_2_out, CLK, nand_1_out);
  nand nand_3 (Q, nand_1_out, nand_4_out);
  nand nand_4 (nand_4_out, Q, nand_2_out);
endmodule
