// Logisim project LabWeek7.circ as structural Verilog: 8 circuits, main circuit Multiplier!
module mulData (
  input  [7:0] X,
  input  [7:0] Y,
  input  [2:0] i,
  input  [1:0] Q,
  input  [1:0] clk,
  output [7:0] OUT
);

  wire multiplexer_2_out;
  wire [7:0] adder_1_out, multiplexer_1_out, multiplexer_3_out, register_1_q;

  Register #(.trigger("high")) register_1 (.D(OUT), .en(1'b1), .Q(register_1_q), .clk(clk[1]));  // open: clr
  Adder adder_1 (.a({register_1_q[6:0], 1'b0}), .b(X), .out(adder_1_out), .cin(1'b0));  // open: cout
  Multiplexer #(.width(8), .enable("false")) multiplexer_1 (
    .in0({register_1_q[6:0], 1'b0}), .in1(adder_1_out), .out(multiplexer_1_out), .sel(multiplexer_2_out));
  Multiplexer #(.select(3), .enable("false")) multiplexer_2 (
    .in0(Y[7]), .in1(Y[6]), .in2(Y[5]), .in3(Y[4]), .in4(Y[3]), .in5(Y[2]), .in6(Y[1]), .in7(Y[0]),
    .out(multiplexer_2_out), .sel(i));
  Multiplexer #(.select(2), .width(8), .enable("false")) multiplexer_3 (
    .in0({8{1'b0}}), .in1({8{1'b0}}), .in2(multiplexer_1_out), .in3(register_1_q), .out(multiplexer_3_out),
    .sel(Q));
  Register #(.trigger("high")) register_2 (.D(multiplexer_3_out), .en(1'b1), .Q(OUT), .clk(clk[0]));  // open: clr
  Hex_Digit_Display hex_digit_display_1 (.value(OUT[7:4]));  // open: dp
  Hex_Digit_Display hex_digit_display_2 (.value(OUT[3:0]));  // open: dp
endmodule

// CLK
module clk_2phase (
  output phi_1,
  output phi_2
);

  wire clock_1_out, nand_1_out, nand_2_out, not_1_out, not_2_out, not_3_out;

  Clock clock_1 (.out(clock_1_out));
  not not_1 (not_1_out, clock_1_out);
  nand nand_1 (nand_1_out, not_1_out, phi_2);
  not not_2 (not_2_out, nand_1_out);
  not not_3 (not_3_out, nand_2_out);
  nand nand_2 (nand_2_out, phi_1, clock_1_out);
  not not_4 (phi_1, not_2_out);
  not not_5 (phi_2, not_3_out);
endmodule

module NANDLatch (
  input  D,
  input  CLK,
  output OUT
);

  wire nand_1_out, nand_2_out, nand_4_out;

  nand nand_1 (nand_1_out, D, CLK);
  nand nand_2 (nand_2_out, nand_1_out, CLK);
  nand nand_3 (OUT, nand_1_out, nand_4_out);
  nand nand_4 (nand_4_out, OUT, nand_2_out);
endmodule

module LoopDataPath (
  input  [3:0] N,
  input  [3:0] M,
  input  [1:0] Q,
  input  [1:0] CLK,
  output cmp,
  output [3:0] out_6
);

  wire [3:0] adder_1_out, multiplexer_1_out, nandlatch_5_out;

  NANDLatch nandlatch_1 (.D(nandlatch_5_out[0]), .CLK(CLK[0]), .OUT(out_6[0]));
  NANDLatch nandlatch_2 (.D(nandlatch_5_out[1]), .CLK(CLK[0]), .OUT(out_6[1]));
  NANDLatch nandlatch_3 (.D(nandlatch_5_out[2]), .CLK(CLK[0]), .OUT(out_6[2]));
  NANDLatch nandlatch_4 (.D(nandlatch_5_out[3]), .CLK(CLK[0]), .OUT(out_6[3]));
  Comparator #(.width(4), .mode("unsigned")) comparator_1 (.a(adder_1_out), .b(N), .lt(cmp));  // open: gt, eq
  Adder #(.width(4)) adder_1 (.a(4'b0001), .b(out_6), .out(adder_1_out), .cin(1'b0));  // open: cout
  Multiplexer #(.select(2), .width(4), .enable("false")) multiplexer_1 (
    .in0(4'b0000), .in1(M), .in2(adder_1_out), .in3(out_6), .out(multiplexer_1_out), .sel(Q));
  NANDLatch nandlatch_5 (.D(multiplexer_1_out[0]), .CLK(CLK[1]), .OUT(nandlatch_5_out[0]));
  NANDLatch nandlatch_6 (.D(multiplexer_1_out[1]), .CLK(CLK[1]), .OUT(nandlatch_5_out[1]));
  NANDLatch nandlatch_7 (.D(multiplexer_1_out[2]), .CLK(CLK[1]), .OUT(nandlatch_5_out[2]));
  NANDLatch nandlatch_8 (.D(multiplexer_1_out[3]), .CLK(CLK[1]), .OUT(nandlatch_5_out[3]));
endmodule

module LoopControl (
  input  req,
  input  [1:0] Q,
  input  cmp,
  output [1:0] Q_prime
);

  wire and_1_out, and_2_out, and_3_out, and_4_out, and_5_out;

  and and_1 (and_1_out, req, ~Q[0], ~Q[1]);  // AND_Gate
  and and_2 (and_2_out, req, Q[0], Q[1]);
  and and_3 (and_3_out, req, Q[1], ~cmp);  // AND_Gate
  and and_4 (and_4_out, req, Q[0]);
  and and_5 (and_5_out, req, Q[1]);
  or or_1 (Q_prime[0], and_1_out, and_2_out, and_3_out);
  or or_2 (Q_prime[1], and_4_out, and_5_out);
endmodule

module Multiplier (
  input  [7:0] X,
  input  [7:0] Y,
  input  in_3,
  output [3:0] out_4,
  output [7:0] out_5,
  output ACK
);

  wire loopdatapath_1_cmp;
  wire [1:0] clk_2phase_1_phi_1, loopcontrol_1_q_prime, nandlatch_1_out, nandlatch_2_out;

  mulData muldata_1 (.X(X), .Y(Y), .clk(clk_2phase_1_phi_1), .i(out_4[2:0]), .Q(nandlatch_2_out), .OUT(out_5));
  LoopDataPath loopdatapath_1 (
    .N(4'b1000), .M(4'b0000), .Q(nandlatch_2_out), .out_6(out_4), .CLK(clk_2phase_1_phi_1),
    .cmp(loopdatapath_1_cmp));
  NANDLatch nandlatch_1 (.D(loopcontrol_1_q_prime[0]), .CLK(clk_2phase_1_phi_1[1]), .OUT(nandlatch_1_out[0]));
  LoopControl loopcontrol_1 (
    .req(in_3), .Q(nandlatch_2_out), .cmp(loopdatapath_1_cmp), .Q_prime(loopcontrol_1_q_prime));
  NANDLatch nandlatch_2 (.D(nandlatch_1_out[0]), .CLK(clk_2phase_1_phi_1[0]), .OUT(nandlatch_2_out[0]));
  NANDLatch nandlatch_3 (.D(loopcontrol_1_q_prime[1]), .CLK(clk_2phase_1_phi_1[1]), .OUT(nandlatch_1_out[1]));
  NANDLatch nandlatch_4 (.D(nandlatch_1_out[1]), .CLK(clk_2phase_1_phi_1[0]), .OUT(nandlatch_2_out[1]));
  clk_2phase clk_2phase_1 (.phi_1(clk_2phase_1_phi_1[0]), .phi_2(clk_2phase_1_phi_1[1]));
  and and_1 (ACK, nandlatch_2_out[0], nandlatch_2_out[1]);
  Hex_Digit_Display hex_digit_display_1 (.value(out_5[7:4]));  // open: dp
  Hex_Digit_Display hex_digit_display_2 (.value(out_5[3:0]));  // open: dp

  // Other names for the same wires on the sheet: OUT[7:0] = out_5
endmodule

module Tree_Multiplier (
  input  [3:0] X,
  input  [3:0] Y
);

  wire [3:0] and_1_out;
  wire [4:1] and_6_out;
  wire [5:2] and_9_out;
  wire [6:3] and_14_out;
  wire [7:0] adder_1_out, adder_2_out, adder_3_out;

  and and_1 (and_1_out[0], X[0], Y[0]);
  and and_2 (and_1_out[1], X[1], Y[0]);
  and and_3 (and_1_out[3], X[3], Y[0]);
  and and_4 (and_1_out[2], X[2], Y[0]);
  and and_5 (and_6_out[2], X[1], Y[1]);
  and and_6 (and_6_out[1], X[0], Y[1]);
  Adder adder_1 (.a({3'b000, and_6_out, 1'b0}), .b({4'b0000, and_1_out}), .out(adder_1_out), .cin(1'b0));  // open: cout
  and and_7 (and_6_out[3], X[2], Y[1]);
  and and_8 (and_6_out[4], X[3], Y[1]);
  and and_9 (and_9_out[2], X[0], Y[2]);
  and and_10 (and_9_out[3], X[1], Y[2]);
  Adder adder_2 (.a(adder_3_out), .b(adder_1_out), .out(adder_2_out), .cin(1'b0));  // open: cout
  and and_11 (and_9_out[4], X[2], Y[2]);
  and and_12 (and_9_out[5], X[3], Y[2]);
  Hex_Digit_Display hex_digit_display_1 (.value(adder_2_out[7:4]));  // open: dp
  Hex_Digit_Display hex_digit_display_2 (.value(adder_2_out[3:0]));  // open: dp
  and and_13 (and_14_out[4], X[1], Y[3]);
  and and_14 (and_14_out[3], X[0], Y[3]);
  Adder adder_3 (
    .a({1'b0, and_14_out, 3'b000}), .b({2'b00, and_9_out, 2'b00}), .out(adder_3_out), .cin(1'b0));  // open: cout
  and and_15 (and_14_out[5], X[2], Y[3]);
  and and_16 (and_14_out[6], X[3], Y[3]);
endmodule

module TEST (
  input  [7:0] in_1,
  input  [7:0] in_2,
  input  in_3
);

  wire multiplier_1_ack;
  wire [3:0] multiplier_1_out_4;
  wire [7:0] multiplier_1_out_5;

  Hex_Digit_Display hex_digit_display_1 (.value(multiplier_1_out_4));  // open: dp
  Multiplier multiplier_1 (
    .X(in_1), .Y(in_2), .in_3(in_3), .out_4(multiplier_1_out_4), .out_5(multiplier_1_out_5),
    .ACK(multiplier_1_ack));
  Hex_Digit_Display hex_digit_display_2 (.value(multiplier_1_out_5[7:4]));  // open: dp
  Hex_Digit_Display hex_digit_display_3 (.value(multiplier_1_out_5[3:0]), .dp(multiplier_1_ack));

  // Notes on the sheet:
  //   i
endmodule
