// Logisim project iterativemultROM.circ as structural Verilog: 2 circuits, main circuit main
module main (
  input  req,
  input  [7:0] X,
  input  [7:0] Y,
  output cmp,
  output ack
);

  wire clk_phi_1, clk_phi_2, multiplexer_3_out;
  wire [1:0] Q, Q_prime, register_1_q;
  wire [2:0] bit_extender_1_out;
  wire [3:0] adder_1_out, i, i_prime, multiplexer_1_out;
  wire [7:0] adder_2_out, multiplexer_2_out, multiplexer_4_out, multiplexer_5_out, R, R_prime, shifter_1_out;

  Register #(.width(4), .trigger("high")) u_i (.D(i_prime), .Q(i), .clk(clk_phi_2));  // open: en, clr
  Register #(.width(2), .trigger("high")) register_1 (.D(Q_prime), .Q(register_1_q), .clk(clk_phi_2));  // open: en, clr
  Register #(.trigger("high")) u_R (.D(R_prime), .Q(R), .clk(clk_phi_2));  // open: en, clr
  Comparator #(.width(4), .mode("unsigned")) comparator_1 (.a(i), .b(4'b1000), .lt(cmp));  // open: gt, eq
  Shifter shifter_1 (.in(R), .\dist (3'b001), .out(shifter_1_out));
  clk clk (.phi_1(clk_phi_1), .phi_2(clk_phi_2));
  Adder #(.width(4)) adder_1 (.a(i), .b(4'b0001), .out(adder_1_out), .cin(1'b0));  // open: cout
  Adder adder_2 (.a(shifter_1_out), .b(X), .out(adder_2_out));  // open: cin, cout
  Bit_Extender #(.in_width(4), .out_width(3)) bit_extender_1 (.in(i), .out(bit_extender_1_out));
  Multiplexer #(.select(2), .width(4), .enable("false")) multiplexer_1 (
    .in0(4'b0000), .in1(4'b0000), .in2(adder_1_out), .in3(i), .out(multiplexer_1_out), .sel(Q));
  ROM #(.addrWidth(4), .dataWidth(3)) rom_1 (.addr({req, cmp, register_1_q}), .data({Q, ack}));  // open: sel
  Multiplexer #(.width(8), .enable("false")) multiplexer_2 (
    .in0(shifter_1_out), .in1(adder_2_out), .out(multiplexer_2_out), .sel(multiplexer_3_out));
  Multiplexer #(.select(3), .enable("false")) multiplexer_3 (
    .in0(Y[7]), .in1(Y[6]), .in2(Y[5]), .in3(Y[4]), .in4(Y[3]), .in5(Y[2]), .in6(Y[1]), .in7(Y[0]),
    .out(multiplexer_3_out), .sel(bit_extender_1_out));
  Multiplexer #(.select(2), .width(8), .enable("false")) multiplexer_4 (
    .in0({8{1'b0}}), .in1({8{1'b0}}), .in2(multiplexer_2_out), .in3(R), .out(multiplexer_4_out), .sel(Q));
  Register #(.width(4), .trigger("high")) u_i_prime (
    .D(multiplexer_1_out), .Q(i_prime), .clk(clk_phi_1));  // open: en, clr
  Register #(.width(2), .trigger("high")) register_2 (.D(Q), .Q(Q_prime), .clk(clk_phi_1));  // open: en, clr
  Register #(.trigger("high")) u_R_prime (.D(multiplexer_4_out), .Q(R_prime), .clk(clk_phi_1));  // open: en, clr
  // Probe on multiplexer_5_out
  Multiplexer #(.width(8), .enable("false")) multiplexer_5 (
    .in0({8{1'b0}}), .in1(R), .out(multiplexer_5_out), .sel(ack));

  // Notes on the sheet:
  //   contents of rom_1 (hex, n*v repeats v):
  //   0 0 0 1 0 0 0 1 2 4 6 7 2 4 4 7
endmodule

module clk (
  output phi_1,
  output phi_2
);

  wire clock_1_out, nand_1_out, nand_2_out, not_1_out, not_2_out, not_3_out;

  Clock clock_1 (.out(clock_1_out));
  not not_1 (not_1_out, clock_1_out);
  nand nand_1 (nand_1_out, not_1_out, phi_2);
  not not_2 (not_2_out, nand_1_out);
  nand nand_2 (nand_2_out, phi_1, clock_1_out);
  not not_3 (not_3_out, nand_2_out);
  not not_4 (phi_1, not_2_out);
  not not_5 (phi_2, not_3_out);
endmodule
