// Logisim project lab-7.s.circ as structural Verilog: 5 circuits, main circuit clk_2phase
module main (
  input  [3:0] m,
  input  [3:0] n,
  input  req,
  input  [7:0] x,
  input  [7:0] y,
  input  [7:0] x_2,
  input  [7:0] y_2,
  input  req_2
);

  wire clk_2phase_1_phi_1, clk_2phase_1_phi_2, clk_2phase_2_phi_1, clk_2phase_2_phi_2, ctr_4bit_1_ack,
       mul_8bit_iterative_1_ack;
  wire [1:0] ctr_4bit_1_q;
  wire [3:0] ctr_4bit_1_i;
  wire [7:0] mul_8bit_combinatorial_1_r, mul_8bit_iterative_1_r;

  clk_2phase clk_2phase_1 (.phi_1(clk_2phase_1_phi_1), .phi_2(clk_2phase_1_phi_2));
  clk_2phase clk_2phase_2 (.phi_1(clk_2phase_2_phi_1), .phi_2(clk_2phase_2_phi_2));
  // Probe on ctr_4bit_1_q
  // Probe on ctr_4bit_1_i
  ctr_4bit ctr_4bit_1 (
    .req(req), .Q(ctr_4bit_1_q), .ack(ctr_4bit_1_ack), .i(ctr_4bit_1_i), .phi_1(clk_2phase_1_phi_1),
    .phi_2(clk_2phase_1_phi_2), .m(m), .n(n));
  // Probe on ctr_4bit_1_ack
  // Probe on mul_8bit_combinatorial_1_r
  mul_8bit_combinatorial mul_8bit_combinatorial_1 (.x(x), .y(y), .r(mul_8bit_combinatorial_1_r));
  // Probe on mul_8bit_iterative_1_r
  mul_8bit_iterative mul_8bit_iterative_1 (
    .req(req_2), .x(x_2), .ack(mul_8bit_iterative_1_ack), .r(mul_8bit_iterative_1_r), .y(y_2),
    .phi_1(clk_2phase_2_phi_1), .phi_2(clk_2phase_2_phi_2));
  // Probe on mul_8bit_iterative_1_ack
endmodule

// CLK
module clk_2phase (
  output phi_1,
  output phi_2
);

  wire clock_1_out, nand_1_out, nand_2_out, not_1_out, not_2_out, not_3_out;

  Clock clock_1 (.out(clock_1_out));
  not not_1 (not_1_out, clock_1_out);
  nand nand_1 (nand_1_out, not_1_out, phi_2);
  not not_2 (not_2_out, nand_1_out);
  not not_3 (not_3_out, nand_2_out);
  nand nand_2 (nand_2_out, phi_1, clock_1_out);
  not not_4 (phi_1, not_2_out);
  not not_5 (phi_2, not_3_out);
endmodule

// CTR
module ctr_4bit (
  input  req,
  input  [3:0] n,
  input  [3:0] m,
  input  phi_1,
  input  phi_2,
  output [1:0] Q,
  output ack,
  output [3:0] i
);

  wire and_1_out, and_2_out, and_3_out, and_4_out, and_5_out, cmp, not_1_out, not_2_out, not_3_out, not_4_out;
  wire [1:0] or_2_out, Q_prime;
  wire [3:0] adder_1_out, i_prime, multiplexer_1_out;

  Register #(.width(2), .trigger("high")) u_Q (.D(Q_prime), .Q(Q), .clk(phi_1));  // open: en, clr
  Register #(.width(4), .trigger("high")) u_i (.D(i_prime), .Q(i), .clk(phi_1));  // open: en, clr
  not not_1 (not_1_out, Q[0]);
  not not_2 (not_2_out, Q[1]);
  not not_3 (not_3_out, cmp);
  not not_4 (not_4_out, req);
  and and_1 (and_1_out, req, Q[0]);
  and and_2 (and_2_out, req, Q[1]);
  or or_1 (or_2_out[1], and_1_out, and_2_out);
  Comparator #(.width(4), .mode("unsigned")) comparator_1 (.a(adder_1_out), .b(n), .lt(cmp));  // open: gt, eq
  Adder #(.width(4)) adder_1 (.a(4'b0001), .b(i), .out(adder_1_out));  // open: cin, cout
  and and_3 (and_3_out, req, not_2_out, not_1_out);
  and and_4 (and_4_out, req, Q[1], Q[0]);
  or or_2 (or_2_out[0], and_3_out, and_4_out, and_5_out);
  and and_5 (and_5_out, req, not_3_out, Q[1]);
  and and_6 (ack, Q[1], Q[0]);
  Register #(.width(2), .trigger("high")) u_Q_prime (.D(or_2_out), .Q(Q_prime), .clk(phi_2));  // open: en, clr
  Register #(.width(4), .trigger("high")) u_i_prime (.D(multiplexer_1_out), .Q(i_prime), .clk(phi_2));  // open: en, clr
  Multiplexer #(.select(2), .width(4), .enable("false")) multiplexer_1 (
    .in0(4'b0000), .in1(m), .in2(adder_1_out), .in3(i), .out(multiplexer_1_out), .sel(Q));
endmodule

// MUL
module mul_8bit_combinatorial (
  input  [7:0] x,
  input  [7:0] y,
  output [7:0] r
);

  wire [7:0] adder_1_out, adder_2_out, adder_3_out, adder_4_out, adder_5_out, adder_6_out, and_1_out,
       and_2_out, and_3_out, and_4_out, and_5_out, and_6_out, and_7_out, and_8_out, bit_extender_1_out,
       bit_extender_2_out, bit_extender_3_out, bit_extender_4_out, bit_extender_5_out, bit_extender_6_out,
       bit_extender_7_out, bit_extender_8_out, shifter_1_out, shifter_2_out, shifter_3_out, shifter_4_out,
       shifter_5_out, shifter_6_out, shifter_7_out, shifter_8_out;

  assign bit_extender_1_out = {{7{y[0]}}, y[0]};  // Bit_Extender bit_extender_1
  assign bit_extender_2_out = {{7{y[1]}}, y[1]};  // Bit_Extender bit_extender_2
  assign bit_extender_3_out = {{7{y[2]}}, y[2]};  // Bit_Extender bit_extender_3
  assign bit_extender_4_out = {{7{y[3]}}, y[3]};  // Bit_Extender bit_extender_4
  assign bit_extender_5_out = {{7{y[4]}}, y[4]};  // Bit_Extender bit_extender_5
  assign bit_extender_6_out = {{7{y[5]}}, y[5]};  // Bit_Extender bit_extender_6
  assign bit_extender_7_out = {{7{y[6]}}, y[6]};  // Bit_Extender bit_extender_7
  assign bit_extender_8_out = {{7{y[7]}}, y[7]};  // Bit_Extender bit_extender_8
  assign and_1_out = x & bit_extender_1_out;  // AND_Gate and_1, 8 bits wide
  assign and_2_out = x & bit_extender_2_out;  // AND_Gate and_2, 8 bits wide
  assign and_3_out = x & bit_extender_3_out;  // AND_Gate and_3, 8 bits wide
  assign and_4_out = x & bit_extender_4_out;  // AND_Gate and_4, 8 bits wide
  assign and_5_out = x & bit_extender_5_out;  // AND_Gate and_5, 8 bits wide
  assign and_6_out = x & bit_extender_6_out;  // AND_Gate and_6, 8 bits wide
  assign and_7_out = x & bit_extender_7_out;  // AND_Gate and_7, 8 bits wide
  assign and_8_out = x & bit_extender_8_out;  // AND_Gate and_8, 8 bits wide
  Shifter shifter_1 (.in(and_1_out), .\dist (3'b000), .out(shifter_1_out));
  Shifter shifter_2 (.in(and_2_out), .\dist (3'b001), .out(shifter_2_out));
  Shifter shifter_3 (.in(and_3_out), .\dist (3'b010), .out(shifter_3_out));
  Shifter shifter_4 (.in(and_4_out), .\dist (3'b011), .out(shifter_4_out));
  Shifter shifter_5 (.in(and_5_out), .\dist (3'b100), .out(shifter_5_out));
  Shifter shifter_6 (.in(and_6_out), .\dist (3'b101), .out(shifter_6_out));
  Shifter shifter_7 (.in(and_7_out), .\dist (3'b110), .out(shifter_7_out));
  Shifter shifter_8 (.in(and_8_out), .\dist (3'b111), .out(shifter_8_out));
  Adder adder_1 (.a(shifter_1_out), .b(shifter_2_out), .out(adder_1_out));  // open: cin, cout
  Adder adder_2 (.a(shifter_3_out), .b(shifter_4_out), .out(adder_2_out));  // open: cin, cout
  Adder adder_3 (.a(shifter_5_out), .b(shifter_6_out), .out(adder_3_out));  // open: cin, cout
  Adder adder_4 (.a(shifter_7_out), .b(shifter_8_out), .out(adder_4_out));  // open: cin, cout
  Adder adder_5 (.a(adder_1_out), .b(adder_2_out), .out(adder_5_out));  // open: cin, cout
  Adder adder_6 (.a(adder_3_out), .b(adder_4_out), .out(adder_6_out));  // open: cin, cout
  Adder adder_7 (.a(adder_5_out), .b(adder_6_out), .out(r));  // open: cin, cout
endmodule

// MUL
module mul_8bit_iterative (
  input  req,
  input  [7:0] x,
  input  [7:0] y,
  input  phi_1,
  input  phi_2,
  output ack,
  output [7:0] r
);

  wire [1:0] Q;
  wire [7:0] adder_1_out, multiplexer_1_out, multiplexer_2_out, multiplexer_3_out, multiplexer_4_out,
       shifter_1_out, shifter_2_out, t_prime, x_prime, x_q, y_prime, y_q;

  ctr_4bit i (.req(req), .Q(Q), .ack(ack), .phi_1(phi_1), .phi_2(phi_2), .m(4'b0000), .n(4'b1000));  // open: i
  Register #(.trigger("high")) t (.D(t_prime), .Q(r), .clk(phi_1));  // open: en, clr
  Register #(.trigger("high")) u_x (.D(x_prime), .Q(x_q), .clk(phi_1));  // open: en, clr
  Register #(.trigger("high")) u_y (.D(y_prime), .Q(y_q), .clk(phi_1));  // open: en, clr
  Shifter shifter_1 (.in(r), .\dist (3'b001), .out(shifter_1_out));
  Adder adder_1 (.a(shifter_1_out), .b(x_q), .out(adder_1_out));  // open: cin, cout
  Shifter shifter_2 (.in(y_q), .\dist (3'b001), .out(shifter_2_out));
  Multiplexer #(.width(8), .enable("false")) multiplexer_1 (
    .in0(shifter_1_out), .in1(adder_1_out), .out(multiplexer_1_out), .sel(y_q[7]));
  Multiplexer #(.select(2), .width(8), .enable("false")) multiplexer_2 (
    .in0({8{1'b0}}), .in1({8{1'b0}}), .in2(multiplexer_1_out), .in3(r), .out(multiplexer_2_out), .sel(Q));
  Multiplexer #(.select(2), .width(8), .enable("false")) multiplexer_3 (
    .in0({8{1'b0}}), .in1(x), .in2(x_q), .in3(x_q), .out(multiplexer_3_out), .sel(Q));
  Multiplexer #(.select(2), .width(8), .enable("false")) multiplexer_4 (
    .in0({8{1'b0}}), .in1(y), .in2(shifter_2_out), .in3(y_q), .out(multiplexer_4_out), .sel(Q));
  Register #(.trigger("high")) u_t_prime (.D(multiplexer_2_out), .Q(t_prime), .clk(phi_2));  // open: en, clr
  Register #(.trigger("high")) u_x_prime (.D(multiplexer_3_out), .Q(x_prime), .clk(phi_2));  // open: en, clr
  // Probe on x_q
  Register #(.trigger("high")) u_y_prime (.D(multiplexer_4_out), .Q(y_prime), .clk(phi_2));  // open: en, clr
  // Probe on y_q
endmodule
