// Logisim project Shifter4bits.circ as structural Verilog: 1 circuit, main circuit main
module main (
  input  Shift_2_bits,
  input  Shift_1_bit,
  input  in_3,
  input  in_4,
  input  in_5,
  input  in_6,
  output out_7,
  output out_8,
  output out_9,
  output out_10
);

  wire [3:0] multiplexer_2_out;

  Multiplexer #(.width(4)) multiplexer_1 (
    .in0(multiplexer_2_out), .in1({multiplexer_2_out[1:0], 2'b00}), .out({out_7, out_8, out_9, out_10}),
    .sel(Shift_2_bits));  // open: en
  Multiplexer #(.width(4)) multiplexer_2 (
    .in0({in_3, in_4, in_5, in_6}), .in1({in_4, in_5, in_6, 1'b0}), .out(multiplexer_2_out), .sel(Shift_1_bit));  // open: en

  // Notes on the sheet:
  //   Not-Shifted
  //   Shifted
endmodule
