// Logisim project lab-8_s.circ as structural Verilog: 5 circuits, main circuit main
module main (
);

  wire clk_2phase_1_phi_1, clk_2phase_1_phi_2, hp35_c_t_1_append, hp35_c_t_1_en_1, hp35_c_t_1_en_2,
       hp35_c_t_1_raise;
  wire [2:0] hp35_rom_1_c_alu, hp35_rom_1_c_s, hp35_rom_1_c_t, hp35_rom_1_c_x, hp35_rom_1_c_y, hp35_rom_1_c_z;
  wire [4:0] hp35_c_t_1_c;
  wire [7:0] hp35_a_r_1_s, hp35_a_r_1_t, hp35_a_r_1_x, hp35_a_r_1_y, hp35_a_r_1_z, hp35_c_t_1_v;
  wire [31:0] _0_out;

  Button button (.out(_0_out[16]));
  Button CLR (.out(_0_out[20]));
  Button STO (.out(_0_out[21]));
  Button button_2 (.out(_0_out[17]));
  Button button_3 (.out(_0_out[18]));
  Button RCL (.out(_0_out[22]));
  Button button_4 (.out(_0_out[23]));
  Button button_5 ();  // open: out
  Button _7 (.out(_0_out[7]));
  Button _8 (.out(_0_out[8]));
  Button _9 (.out(_0_out[9]));
  Button _6 (.out(_0_out[6]));
  Button _4 (.out(_0_out[4]));
  Button _5 (.out(_0_out[5]));
  Button _2 (.out(_0_out[2]));
  Button _1 (.out(_0_out[1]));
  Button _3 (.out(_0_out[3]));
  Button _0 (.out(_0_out[0]));
  Button button_6 ();  // open: out
  Button button_7 ();  // open: out
  hp35_ROM hp35_rom_1 (
    .C(hp35_c_t_1_c), .append(hp35_c_t_1_append), .raise(hp35_c_t_1_raise), .c_Z(hp35_rom_1_c_z),
    .c_Y(hp35_rom_1_c_y), .c_S(hp35_rom_1_c_s), .c_ALU(hp35_rom_1_c_alu), .c_T(hp35_rom_1_c_t),
    .c_X(hp35_rom_1_c_x));
  hp35_C_T hp35_c_t_1 (
    .K(_0_out), .phi_1(clk_2phase_1_phi_1), .phi_2(clk_2phase_1_phi_2), .en_1(hp35_c_t_1_en_1),
    .en_2(hp35_c_t_1_en_2), .C(hp35_c_t_1_c), .append(hp35_c_t_1_append), .raise(hp35_c_t_1_raise),
    .V(hp35_c_t_1_v));  // open: in_2
  clk_2phase clk_2phase_1 (.phi_1(clk_2phase_1_phi_1), .phi_2(clk_2phase_1_phi_2));
  hp35_A_R hp35_a_r_1 (
    .c_ALU(hp35_rom_1_c_alu), .V(hp35_c_t_1_v), .X(hp35_a_r_1_x), .Y(hp35_a_r_1_y), .Z(hp35_a_r_1_z),
    .T(hp35_a_r_1_t), .S(hp35_a_r_1_s), .c_X(hp35_rom_1_c_x), .c_Y(hp35_rom_1_c_y), .c_Z(hp35_rom_1_c_z),
    .c_T(hp35_rom_1_c_t), .c_S(hp35_rom_1_c_s), .en_1(hp35_c_t_1_en_1), .en_2(hp35_c_t_1_en_2));
  // Probe on hp35_a_r_1_x
  // Probe on hp35_a_r_1_y
  // Probe on hp35_a_r_1_z
  // Probe on hp35_a_r_1_t
  // Probe on hp35_a_r_1_s
endmodule

// CLK
module clk_2phase (
  output phi_1,
  output phi_2
);

  wire clock_1_out, nand_1_out, nand_2_out, not_1_out, not_2_out, not_3_out;

  Clock clock_1 (.out(clock_1_out));
  not not_1 (not_1_out, clock_1_out);
  nand nand_1 (nand_1_out, not_1_out, phi_2);
  not not_2 (not_2_out, nand_1_out);
  not not_3 (not_3_out, nand_2_out);
  nand nand_2 (nand_2_out, phi_1, clock_1_out);
  not not_4 (phi_1, not_2_out);
  not not_5 (phi_2, not_3_out);
endmodule

// A&R
module hp35_A_R (
  input  [7:0] V,
  input  [2:0] c_ALU,
  input  [2:0] c_X,
  input  [2:0] c_Y,
  input  [2:0] c_Z,
  input  [2:0] c_T,
  input  [2:0] c_S,
  input  en_1,
  input  en_2,
  output [7:0] X,
  output [7:0] Y,
  output [7:0] Z,
  output [7:0] T,
  output [7:0] S
);

  wire adder_1_cout, adder_2_cout, multiplexer_7_out, subtractor_1_bout;
  wire [7:0] adder_1_out, adder_2_out, multiplexer_1_out, multiplexer_2_out, multiplexer_3_out,
       multiplexer_4_out, multiplexer_5_out, multiplexer_6_out, multiplier_1_out, R, S_prime,
       subtractor_1_out, T_prime, X_prime, Y_prime, Z_prime;

  Multiplexer #(.width(8), .enable("false")) multiplexer_1 (
    .in0(8'ha), .in1(Y), .out(multiplexer_1_out), .sel(c_ALU[2]));
  Register u_X (.D(X_prime), .Q(X), .clk(en_1));  // open: en, clr
  Register u_Y (.D(Y_prime), .Q(Y), .clk(en_1));  // open: en, clr
  Register u_Z (.D(Z_prime), .Q(Z), .clk(en_1));  // open: en, clr
  Register u_T (.D(T_prime), .Q(T), .clk(en_1));  // open: en, clr
  Register u_S (.D(S_prime), .Q(S), .clk(en_1));  // open: en, clr
  Adder adder_1 (.a(multiplexer_1_out), .b(X), .out(adder_1_out), .cin(1'b0), .cout(adder_1_cout));
  Subtractor subtractor_1 (.a(multiplexer_1_out), .b(X), .out(subtractor_1_out), .bin(1'b0), .bout(subtractor_1_bout));
  Multiplier multiplier_1 (.a(multiplexer_1_out), .b(X), .out(multiplier_1_out), .cin({8{1'b0}}));  // open: cout
  Adder adder_2 (.a(multiplier_1_out), .b(V), .out(adder_2_out), .cin(1'b0), .cout(adder_2_cout));
  Multiplexer #(.select(3), .width(8), .enable("false")) multiplexer_2 (
    .in0({8{1'b0}}), .in1(V), .in2(R), .in3(X), .in4(Y), .in5(Z), .in6(T), .in7(S), .out(multiplexer_2_out),
    .sel(c_X));
  Multiplexer #(.select(3), .width(8), .enable("false")) multiplexer_3 (
    .in0({8{1'b0}}), .in1(V), .in2(R), .in3(X), .in4(Y), .in5(Z), .in6(T), .in7(S), .out(multiplexer_3_out),
    .sel(c_Y));
  Multiplexer #(.select(3), .width(8), .enable("false")) multiplexer_4 (
    .in0({8{1'b0}}), .in1(V), .in2(R), .in3(X), .in4(Y), .in5(Z), .in6(T), .in7(S), .out(multiplexer_4_out),
    .sel(c_Z));
  Multiplexer #(.select(3), .width(8), .enable("false")) multiplexer_5 (
    .in0({8{1'b0}}), .in1(V), .in2(R), .in3(X), .in4(Y), .in5(Z), .in6(T), .in7(S), .out(multiplexer_5_out),
    .sel(c_T));
  Multiplexer #(.select(3), .width(8), .enable("false")) multiplexer_6 (
    .in0({8{1'b0}}), .in1(V), .in2(R), .in3(X), .in4(Y), .in5(Z), .in6(T), .in7(S), .out(multiplexer_6_out),
    .sel(c_S));
  Register u_X_prime (.D(multiplexer_2_out), .Q(X_prime), .clk(en_2));  // open: en, clr
  Register u_Y_prime (.D(multiplexer_3_out), .Q(Y_prime), .clk(en_2));  // open: en, clr
  Register u_Z_prime (.D(multiplexer_4_out), .Q(Z_prime), .clk(en_2));  // open: en, clr
  Register u_T_prime (.D(multiplexer_5_out), .Q(T_prime), .clk(en_2));  // open: en, clr
  Register u_S_prime (.D(multiplexer_6_out), .Q(S_prime), .clk(en_2));  // open: en, clr
  Multiplexer #(.select(2), .enable("false")) multiplexer_7 (
    .in0(adder_1_cout), .in1(subtractor_1_bout), .in2(1'b0), .in3(adder_2_cout), .out(multiplexer_7_out),
    .sel(c_ALU[1:0]));
  // Probe on multiplexer_7_out
  Multiplexer #(.select(2), .width(8), .enable("false")) multiplexer_8 (
    .in0(adder_1_out), .in1(subtractor_1_out), .in2(multiplier_1_out), .in3(adder_2_out), .out(R),
    .sel(c_ALU[1:0]));
endmodule

// C&T
module hp35_C_T (
  input  [31:0] K,
  input  in_2,
  input  phi_1,
  input  phi_2,
  output [7:0] V,
  output [4:0] C,
  output en_2,
  output en_1,
  output append,
  output raise
);

  wire and_1_out, and_2_out, nand_1_out, nand_2_out, not_1_out, not_2_out, not_3_out, not_4_out, not_5_out,
       not_6_out, not_7_out, press, priority_encoder_1_en_out;
  wire [1:0] and_3_out, Q_prime_q;
  wire [3:0] rom_1_data;
  wire [4:0] P, priority_encoder_1_out;
  wire [7:0] bit_extender_2_out;
  wire [9:0] button_1_out;

  Register #(.width(2)) Q (.D(Q_prime_q), .Q({en_1, en_2}), .clk(phi_1));  // open: en, clr
  Priority_Encoder #(.select(5), .disabled(0)) priority_encoder_1 (
    .in0(K[0]), .in1(K[1]), .in2(K[2]), .in3(K[3]), .in4(K[4]), .in5(K[5]), .in6(K[6]), .in7(K[7]),
    .in8(K[8]), .in9(K[9]), .in10(K[10]), .in11(K[11]), .in12(K[12]), .in13(K[13]), .in14(K[14]),
    .in15(K[15]), .in16(K[16]), .in17(K[17]), .in18(K[18]), .in19(K[19]), .in20(K[20]), .in21(K[21]),
    .in22(K[22]), .in23(K[23]), .in24(K[24]), .in25(K[25]), .in26(K[26]), .in27(K[27]), .in28(K[28]),
    .in29(K[29]), .in30(K[30]), .in31(K[31]), .out(priority_encoder_1_out), .gs(press),
    .en_out(priority_encoder_1_en_out));  // open: en_in
  not not_1 (not_1_out, en_2);
  not not_2 (not_2_out, en_1);
  not not_3 (not_3_out, press);
  Register #(.width(5), .trigger("high")) register_1 (.D(priority_encoder_1_out), .Q(C), .clk(press));  // open: en, clr
  and and_1 (and_1_out, press, en_2);
  and and_2 (and_2_out, press, en_1);
  or or_1 (and_3_out[1], and_1_out, and_2_out);
  not not_4 (not_4_out, P[0]);
  not not_5 (not_5_out, P[1]);
  not not_6 (not_6_out, P[2]);
  not not_7 (not_7_out, P[3]);
  not not_8 (append, P[4]);
  Register #(.width(5), .trigger("high")) register_2 (.D(C), .Q(P), .clk(en_1));  // open: en, clr
  and and_3 (and_3_out[0], press, not_1_out, not_2_out);
  nand nand_1 (nand_1_out, P[4], not_7_out, P[2], not_5_out, P[0]);
  and and_4 (raise, P[4], nand_1_out, nand_2_out);
  Register #(.width(2)) Q_prime (.D(and_3_out), .Q(Q_prime_q), .clk(phi_2));  // open: en, clr
  nand nand_2 (nand_2_out, P[4], not_7_out, P[2], P[1], P[0]);
  assign V = {{4{1'b0}}, C[3:0]};  // Bit_Extender bit_extender_1
  assign bit_extender_2_out = {{4{1'b0}}, P[3:0]};  // Bit_Extender bit_extender_2
  // Probe on bit_extender_2_out
  // Probe on P
  Button button_1 (.out(button_1_out[0]));
  Button button_2 (.out(button_1_out[1]));
  Button button_3 (.out(button_1_out[2]));
  Button button_4 (.out(button_1_out[9]));
  ROM #(.addrWidth(10), .dataWidth(4)) rom_1 (
    .addr({{7{button_1_out[9]}}, button_1_out[2:0]}), .data(rom_1_data), .sel(in_2));
  // Probe on rom_1_data

  // Notes on the sheet:
  //   contents of rom_1 (hex, n*v repeats v):
  //   0 1 2 0 3
endmodule

// ROM
module hp35_ROM (
  input  [4:0] C,
  input  append,
  input  raise,
  output [2:0] c_ALU,
  output [2:0] c_X,
  output [2:0] c_Y,
  output [2:0] c_Z,
  output [2:0] c_T,
  output [2:0] c_S
);

  ROM #(.addrWidth(5), .dataWidth(3)) rom_1 (.addr(C), .data(c_ALU));  // open: sel
  ROM #(.addrWidth(7), .dataWidth(3)) rom_2 (.addr({raise, append, C}), .data(c_X));  // open: sel
  ROM #(.addrWidth(7), .dataWidth(3)) rom_3 (.addr({raise, append, C}), .data(c_Y));  // open: sel
  ROM #(.addrWidth(7), .dataWidth(3)) rom_4 (.addr({raise, append, C}), .data(c_Z));  // open: sel
  ROM #(.addrWidth(7), .dataWidth(3)) rom_5 (.addr({raise, append, C}), .data(c_T));  // open: sel
  ROM #(.addrWidth(7), .dataWidth(3)) rom_6 (.addr({raise, append, C}), .data(c_S));  // open: sel

  // Notes on the sheet:
  //   contents of rom_1 (hex, n*v repeats v):
  //   10*3 6*0 4 5 6
  //   contents of rom_2 (hex, n*v repeats v):
  //   10*1 6*0 2 2 2 0 0 3 7 3 8*0 10*2 6*0 2 2 2 0 0 3 7 3 8*0 10*1 6*0 2 2 2 0 0 3 7 3 8*0 10*2 6*0 2 2
  //   2 0 0 3 7 3
  //   contents of rom_3 (hex, n*v repeats v):
  //   10*4 6*0 5 5 5 0 0 4 4 3 8*0 10*4 6*0 5 5 5 0 0 4 4 3 8*0 10*3 6*0 5 5 5 0 0 4 4 3 8*0 10*3 6*0 5 5
  //   5 0 0 4 4 3
  //   contents of rom_4 (hex, n*v repeats v):
  //   10*5 6*0 6 6 6 0 0 5 5 4 8*0 10*5 6*0 6 6 6 0 0 5 5 4 8*0 10*4 6*0 6 6 6 0 0 5 5 4 8*0 10*4 6*0 6 6
  //   6 0 0 5 5 4
  //   contents of rom_5 (hex, n*v repeats v):
  //   10*6 6*0 6 6 6 0 0 6 6 5 8*0 10*6 6*0 6 6 6 0 0 6 6 5 8*0 10*5 6*0 6 6 6 0 0 6 6 5 8*0 10*5 6*0 6 6
  //   6 0 0 6 6 5
  //   contents of rom_6 (hex, n*v repeats v):
  //   10*7 6*0 7 7 7 0 0 3 7 7 8*0 10*7 6*0 7 7 7 0 0 3 7 7 8*0 10*7 6*0 7 7 7 0 0 3 7 7 8*0 10*7 6*0 7 7
  //   7 0 0 3 7 7
endmodule
